// Logisim project logisim.circ as structural Verilog
module adder (
  input  in_1,
  input  in_2,
  input  in_3,
  output out_4,
  output out_5
);

  wire and_1_out, and_2_out, xor_1_out;

  and and_1 (and_1_out, in_1, in_3);
  or or_1 (out_5, and_1_out, and_2_out);
  xor xor_1 (xor_1_out, in_1, in_3);
  xor xor_2 (out_4, xor_1_out, in_2);
  and and_2 (and_2_out, xor_1_out, in_2);
endmodule

// ripple carry adder
module _8_bit_adder (
  input  Cin,
  input  in_2,
  input  _1,
  input  in_4,
  input  _2,
  input  in_6,
  input  _4,
  input  in_8,
  input  _8,
  input  in_10,
  input  _16,
  input  in_12,
  input  _32,
  input  in_14,
  input  _64,
  input  in_16,
  input  _128,
  output out_18,
  output out_19,
  output out_20,
  output out_21,
  output out_22,
  output out_23,
  output out_24,
  output out_25,
  output Cout
);

  wire adder_1_out_5, adder_2_out_5, adder_3_out_5, adder_4_out_5, adder_5_out_5, adder_6_out_5,
       adder_7_out_5;

  adder adder_1 (.in_1(in_2), .in_3(_1), .in_2(Cin), .out_5(adder_1_out_5), .out_4(out_18));
  adder adder_2 (.in_1(in_4), .in_3(_2), .in_2(adder_1_out_5), .out_5(adder_2_out_5), .out_4(out_19));
  adder adder_3 (.in_1(in_6), .in_3(_4), .in_2(adder_2_out_5), .out_5(adder_3_out_5), .out_4(out_20));
  adder adder_4 (.in_1(in_8), .in_3(_8), .in_2(adder_3_out_5), .out_5(adder_4_out_5), .out_4(out_21));
  adder adder_5 (.in_1(in_10), .in_3(_16), .in_2(adder_4_out_5), .out_5(adder_5_out_5), .out_4(out_22));
  adder adder_6 (.in_1(in_12), .in_3(_32), .in_2(adder_5_out_5), .out_5(adder_6_out_5), .out_4(out_23));
  adder adder_7 (.in_1(in_14), .in_3(_64), .in_2(adder_6_out_5), .out_5(adder_7_out_5), .out_4(out_24));
  adder adder_8 (.in_1(in_16), .in_3(_128), .in_2(adder_7_out_5), .out_5(Cout), .out_4(out_25));
endmodule

module _4_bit_multiplexer (
  input  _1,
  input  _2,
  input  _3,
  input  _4,
  output out_5,
  output out_6,
  output out_7,
  output out_8,
  output out_9,
  output out_10,
  output out_11,
  output out_12,
  output out_13,
  output out_14,
  output out_15,
  output out_16,
  output out_17,
  output out_18,
  output out_19,
  output out_20
);

  and _1111 (out_5, _1, _2, _3, _4);
  and _11110 (out_6, _1, _2, _3, ~_4);  // AND_Gate
  and _1101 (out_7, _1, _2, ~_3, _4);  // AND_Gate
  and _1100 (out_8, _1, _2, ~_3, ~_4);  // AND_Gate
  and _1011 (out_9, _1, ~_2, _3, _4);  // AND_Gate
  and _1010 (out_10, _1, ~_2, _3, ~_4);  // AND_Gate
  and _1001 (out_11, _1, ~_2, ~_3, _4);  // AND_Gate
  and _1000 (out_12, _1, ~_2, ~_3, ~_4);  // AND_Gate
  and _0111 (out_13, ~_1, _2, _3, _4);  // AND_Gate
  and _0110 (out_14, ~_1, _2, _3, ~_4);  // AND_Gate
  and _0101 (out_15, ~_1, _2, ~_3, _4);  // AND_Gate
  and _0100 (out_16, ~_1, _2, ~_3, ~_4);  // AND_Gate
  and _0011 (out_17, ~_1, ~_2, _3, _4);  // AND_Gate
  and _0010 (out_18, ~_1, _2, ~_3, ~_4);  // AND_Gate
  and _0001 (out_19, ~_1, ~_2, ~_3, _4);  // AND_Gate
  and _0000 (out_20, ~_1, ~_2, ~_3, ~_4);  // AND_Gate
endmodule

// logical OR
module A___B (
  input  in_1,
  input  in_2,
  input  in_3,
  input  in_4,
  input  in_5,
  input  in_6,
  input  in_7,
  input  in_8,
  input  in_9,
  input  in_10,
  input  in_11,
  input  in_12,
  input  in_13,
  input  in_14,
  input  in_15,
  input  in_16,
  output out_17,
  output out_18,
  output out_19,
  output out_20,
  output out_21,
  output out_22,
  output out_23,
  output out_24
);

  or or_1 (out_17, in_1, in_2);
  or or_2 (out_18, in_3, in_4);
  or or_3 (out_19, in_5, in_6);
  or or_4 (out_20, in_7, in_8);
  or or_5 (out_21, in_9, in_10);
  or or_6 (out_22, in_11, in_12);
  or or_7 (out_23, in_13, in_14);
  or or_8 (out_24, in_15, in_16);
endmodule

// logical AND
module A___B_2 (
  input  in_1,
  input  in_2,
  input  in_3,
  input  in_4,
  input  in_5,
  input  in_6,
  input  in_7,
  input  in_8,
  input  in_9,
  input  in_10,
  input  in_11,
  input  in_12,
  input  in_13,
  input  in_14,
  input  in_15,
  input  in_16,
  output out_17,
  output out_18,
  output out_19,
  output out_20,
  output out_21,
  output out_22,
  output out_23,
  output out_24
);

  and and_1 (out_17, in_1, in_2);
  and and_2 (out_18, in_3, in_4);
  and and_3 (out_19, in_5, in_6);
  and and_4 (out_20, in_7, in_8);
  and and_5 (out_21, in_9, in_10);
  and and_6 (out_22, in_11, in_12);
  and and_7 (out_23, in_13, in_14);
  and and_8 (out_24, in_15, in_16);
endmodule

module circuit (
  input  in_1,
  input  in_2,
  input  in_3,
  input  in_4,
  input  in_5,
  input  in_6,
  input  in_7,
  input  in_8,
  output out_9,
  output out_10,
  output out_11,
  output out_12,
  output out_13,
  output out_14,
  output out_15,
  output out_16
);

  not not_1 (out_9, in_1);
  not not_2 (out_10, in_2);
  not not_3 (out_11, in_3);
  not not_4 (out_12, in_4);
  not not_5 (out_13, in_5);
  not not_6 (out_14, in_6);
  not not_7 (out_15, in_7);
  not not_8 (out_16, in_8);
endmodule

module A_Xor_B (
  input  in_1,
  input  in_2,
  input  in_3,
  input  in_4,
  input  in_5,
  input  in_6,
  input  in_7,
  input  in_8,
  input  in_9,
  input  in_10,
  input  in_11,
  input  in_12,
  input  in_13,
  input  in_14,
  input  in_15,
  input  in_16,
  output out_17,
  output out_18,
  output out_19,
  output out_20,
  output out_21,
  output out_22,
  output out_23,
  output out_24
);

  xor xor_1 (out_17, in_1, in_2);
  xor xor_2 (out_18, in_3, in_4);
  xor xor_3 (out_19, in_5, in_6);
  xor xor_4 (out_20, in_7, in_8);
  xor xor_5 (out_21, in_9, in_10);
  xor xor_6 (out_22, in_11, in_12);
  xor xor_7 (out_23, in_13, in_14);
  xor xor_8 (out_24, in_15, in_16);
endmodule

// blocker
module _8_bit_blocker_ALU (
  input  in_1,
  input  in_2,
  input  in_3,
  input  in_4,
  input  in_5,
  input  in_6,
  input  in_7,
  input  in_8,
  input  in_9,
  input  in_10,
  input  in_11,
  input  in_12,
  input  in_13,
  input  in_14,
  input  in_15,
  input  in_16,
  input  in_17,
  output out_18,
  output out_19,
  output out_20,
  output out_21,
  output out_22,
  output out_23,
  output out_24,
  output out_25,
  output out_26,
  output out_27,
  output out_28,
  output out_29,
  output out_30,
  output out_31,
  output out_32,
  output out_33
);

  and and_1 (out_25, in_9, in_1);
  and and_2 (out_26, in_9, in_10);
  and and_3 (out_24, in_9, in_2);
  and and_4 (out_23, in_9, in_3);
  and and_5 (out_27, in_9, in_11);
  and and_6 (out_28, in_9, in_12);
  and and_7 (out_20, in_9, in_6);
  and and_8 (out_21, in_9, in_5);
  and and_9 (out_22, in_9, in_4);
  and and_10 (out_29, in_9, in_13);
  and and_11 (out_31, in_9, in_15);
  and and_12 (out_30, in_9, in_14);
  and and_13 (out_18, in_9, in_8);
  and and_14 (out_19, in_9, in_7);
  and and_15 (out_32, in_9, in_16);
  and and_16 (out_33, in_9, in_17);
endmodule

module STRtoPAIR (
  input  in_1,
  input  in_2,
  input  in_3,
  input  in_4,
  input  in_5,
  input  in_6,
  input  in_7,
  input  in_8,
  input  in_9,
  input  in_10,
  input  in_11,
  input  in_12,
  input  in_13,
  input  in_14,
  input  in_15,
  input  in_16,
  output out_17,
  output out_18,
  output out_19,
  output out_20,
  output out_21,
  output out_22,
  output out_23,
  output out_24,
  output out_25,
  output out_26,
  output out_27,
  output out_28,
  output out_29,
  output out_30,
  output out_31,
  output out_32
);


  assign out_17 = in_1;
  assign out_18 = in_9;
  assign out_19 = in_2;
  assign out_20 = in_10;
  assign out_21 = in_3;
  assign out_22 = in_11;
  assign out_23 = in_4;
  assign out_24 = in_12;
  assign out_25 = in_5;
  assign out_26 = in_13;
  assign out_27 = in_6;
  assign out_28 = in_14;
  assign out_29 = in_7;
  assign out_30 = in_15;
  assign out_31 = in_8;
  assign out_32 = in_16;
endmodule

module full_sub (
  input  in_1,
  input  in_2,
  input  in_3,
  output out_4,
  output out_5
);

  wire and_1_out, and_2_out, not_1_out, not_2_out, xor_1_out;

  xor xor_1 (xor_1_out, in_2, in_3);
  not not_1 (not_1_out, in_2);
  and and_1 (and_1_out, not_1_out, in_3);
  not not_2 (not_2_out, xor_1_out);
  or or_1 (out_5, and_1_out, and_2_out);
  xor xor_2 (out_4, in_1, xor_1_out);
  and and_2 (and_2_out, not_2_out, in_1);
endmodule

// 8-bit subtractor
module _8_bit_subtractor (
  input  in_1,
  input  in_2,
  input  in_3,
  input  in_4,
  input  in_5,
  input  in_6,
  input  in_7,
  input  in_8,
  input  in_9,
  input  in_10,
  input  in_11,
  input  in_12,
  input  in_13,
  input  in_14,
  input  in_15,
  input  in_16,
  input  in_17,
  output out_18,
  output out_19,
  output out_20,
  output out_21,
  output out_22,
  output out_23,
  output out_24,
  output out_25,
  output out_26
);

  wire full_sub_1_out_5, full_sub_2_out_5, full_sub_3_out_5, full_sub_4_out_5, full_sub_5_out_5,
       full_sub_6_out_5, full_sub_7_out_5;

  full_sub full_sub_1 (.in_2(in_2), .in_3(in_3), .in_1(in_1), .out_5(full_sub_1_out_5), .out_4(out_18));
  full_sub full_sub_2 (.in_2(in_4), .in_3(in_5), .in_1(full_sub_1_out_5), .out_5(full_sub_2_out_5), .out_4(out_19));
  full_sub full_sub_3 (.in_2(in_6), .in_3(in_7), .in_1(full_sub_2_out_5), .out_5(full_sub_3_out_5), .out_4(out_20));
  full_sub full_sub_4 (.in_2(in_8), .in_3(in_9), .in_1(full_sub_3_out_5), .out_5(full_sub_4_out_5), .out_4(out_21));
  full_sub full_sub_5 (.in_2(in_10), .in_3(in_11), .in_1(full_sub_4_out_5), .out_5(full_sub_5_out_5), .out_4(out_22));
  full_sub full_sub_6 (.in_2(in_12), .in_3(in_13), .in_1(full_sub_5_out_5), .out_5(full_sub_6_out_5), .out_4(out_23));
  full_sub full_sub_7 (.in_2(in_14), .in_3(in_15), .in_1(full_sub_6_out_5), .out_5(full_sub_7_out_5), .out_4(out_24));
  full_sub full_sub_8 (.in_2(in_16), .in_3(in_17), .in_1(full_sub_7_out_5), .out_5(out_26), .out_4(out_25));
endmodule

module IF_ODD (
  input  in_1,
  input  in_2,
  input  in_3,
  input  in_4,
  input  in_5,
  input  in_6,
  input  in_7,
  input  in_8,
  output out_9
);

  wire xor_1_out, xor_2_out, xor_3_out, xor_4_out, xor_5_out, xor_6_out;

  xor xor_1 (xor_1_out, in_1, in_2);
  xor xor_2 (xor_2_out, in_3, in_4);
  xor xor_3 (xor_3_out, in_5, in_6);
  xor xor_4 (xor_4_out, in_7, in_8);
  xor xor_5 (xor_5_out, xor_1_out, xor_2_out);
  xor xor_6 (xor_6_out, xor_3_out, xor_4_out);
  xor xor_7 (out_9, xor_5_out, xor_6_out);
endmodule

module blocker_for_bitshifter (
  input  in_1,
  input  in_2,
  input  in_3,
  input  in_4,
  input  in_5,
  input  in_6,
  input  in_7,
  input  in_8,
  input  in_9,
  output out_10,
  output out_11,
  output out_12,
  output out_13,
  output out_14,
  output out_15,
  output out_16,
  output out_17,
  output out_18
);

  and and_1 (out_12, in_2, in_9);
  and and_2 (out_11, in_1, in_9);
  and and_3 (out_14, in_4, in_9);
  and and_4 (out_13, in_3, in_9);
  and and_5 (out_17, in_7, in_9);
  and and_6 (out_16, in_6, in_9);
  and and_7 (out_15, in_5, in_9);
  not not_1 (out_10, in_9);
  and and_8 (out_18, in_8, in_9);
endmodule

module bit_shifter (
  input  in_1,
  input  in_2,
  input  in_3,
  input  in_4,
  input  in_5,
  input  in_6,
  input  in_7,
  input  in_8,
  input  in_9,
  input  in_10,
  input  in_11,
  output out_12,
  output out_13,
  output out_14,
  output out_15,
  output out_16,
  output out_17,
  output out_18,
  output out_19
);

  wire blocker_for_bitshifter_1_out_10, blocker_for_bitshifter_1_out_11, blocker_for_bitshifter_1_out_12,
       blocker_for_bitshifter_1_out_13, blocker_for_bitshifter_1_out_14, blocker_for_bitshifter_1_out_15,
       blocker_for_bitshifter_1_out_16, blocker_for_bitshifter_1_out_17, blocker_for_bitshifter_1_out_18,
       blocker_for_bitshifter_2_out_10, blocker_for_bitshifter_2_out_11, blocker_for_bitshifter_2_out_12,
       blocker_for_bitshifter_2_out_13, blocker_for_bitshifter_2_out_14, blocker_for_bitshifter_2_out_15,
       blocker_for_bitshifter_2_out_16, blocker_for_bitshifter_2_out_17, blocker_for_bitshifter_2_out_18,
       blocker_for_bitshifter_3_out_10, blocker_for_bitshifter_3_out_11, blocker_for_bitshifter_3_out_12,
       blocker_for_bitshifter_3_out_13, blocker_for_bitshifter_3_out_14, blocker_for_bitshifter_3_out_15,
       blocker_for_bitshifter_3_out_16, blocker_for_bitshifter_3_out_17, blocker_for_bitshifter_3_out_18,
       blocker_for_bitshifter_4_out_11, blocker_for_bitshifter_4_out_12, blocker_for_bitshifter_4_out_13,
       blocker_for_bitshifter_4_out_14, blocker_for_bitshifter_4_out_15, blocker_for_bitshifter_4_out_16,
       blocker_for_bitshifter_4_out_17, blocker_for_bitshifter_4_out_18, blocker_for_bitshifter_5_out_11,
       blocker_for_bitshifter_5_out_12, blocker_for_bitshifter_5_out_13, blocker_for_bitshifter_5_out_14,
       blocker_for_bitshifter_5_out_15, blocker_for_bitshifter_5_out_16, blocker_for_bitshifter_5_out_17,
       blocker_for_bitshifter_5_out_18, blocker_for_bitshifter_6_out_11, blocker_for_bitshifter_6_out_12,
       blocker_for_bitshifter_6_out_13, blocker_for_bitshifter_6_out_14, blocker_for_bitshifter_6_out_15,
       blocker_for_bitshifter_6_out_16, blocker_for_bitshifter_6_out_17, blocker_for_bitshifter_6_out_18,
       or_1_out, or_2_out, or_3_out, or_4_out, or_5_out, or_6_out, or_10_out, or_11_out, or_12_out,
       or_13_out, or_14_out, or_15_out, or_18_out, or_19_out, or_20_out, or_21_out, part_1_out_9,
       part_1_out_10, part_1_out_11, part_1_out_12, part_1_out_13, part_1_out_14, part_1_out_15,
       part_1_out_16, part_2_out_9, part_2_out_10, part_2_out_11, part_2_out_12, part_2_out_13,
       part_2_out_14, part_2_out_15, part_2_out_16, part_3_out_9, part_3_out_10, part_3_out_11,
       part_3_out_12, part_3_out_13, part_3_out_14, part_3_out_15, part_3_out_16, part_4_out_9,
       part_4_out_10, part_4_out_11, part_4_out_12, part_4_out_13, part_4_out_14, part_4_out_15,
       part_4_out_16, part_5_out_9, part_5_out_10, part_5_out_11, part_5_out_12, part_5_out_13,
       part_5_out_14, part_5_out_15, part_5_out_16, part_6_out_9, part_6_out_10, part_6_out_11,
       part_6_out_12, part_6_out_13, part_6_out_14, part_6_out_15, part_6_out_16, part_7_out_9,
       part_7_out_10, part_7_out_11, part_7_out_12, part_7_out_13, part_7_out_14, part_7_out_15,
       part_7_out_16;

  circuit_2 part_1 (
    .in_1(blocker_for_bitshifter_1_out_11), .in_2(blocker_for_bitshifter_1_out_12),
    .in_3(blocker_for_bitshifter_1_out_13), .in_4(blocker_for_bitshifter_1_out_14),
    .in_5(blocker_for_bitshifter_1_out_15), .in_6(blocker_for_bitshifter_1_out_16),
    .in_7(blocker_for_bitshifter_1_out_17), .in_8(blocker_for_bitshifter_1_out_18), .out_9(part_1_out_9),
    .out_10(part_1_out_10), .out_11(part_1_out_11), .out_12(part_1_out_12), .out_13(part_1_out_13),
    .out_14(part_1_out_14), .out_15(part_1_out_15), .out_16(part_1_out_16));
  or or_1 (or_1_out, part_1_out_9, blocker_for_bitshifter_4_out_11);
  circuit_2 part_2 (
    .in_1(blocker_for_bitshifter_2_out_11), .in_2(blocker_for_bitshifter_2_out_12),
    .in_3(blocker_for_bitshifter_2_out_13), .in_4(blocker_for_bitshifter_2_out_14),
    .in_5(blocker_for_bitshifter_2_out_15), .in_6(blocker_for_bitshifter_2_out_16),
    .in_7(blocker_for_bitshifter_2_out_17), .in_8(blocker_for_bitshifter_2_out_18), .out_9(part_2_out_9),
    .out_10(part_2_out_10), .out_11(part_2_out_11), .out_12(part_2_out_12), .out_13(part_2_out_13),
    .out_14(part_2_out_14), .out_15(part_2_out_15), .out_16(part_2_out_16));
  circuit_2 part_3 (
    .in_1(part_2_out_9), .in_2(part_2_out_10), .in_3(part_2_out_11), .in_4(part_2_out_12),
    .in_5(part_2_out_13), .in_6(part_2_out_14), .in_7(part_2_out_15), .in_8(part_2_out_16),
    .out_9(part_3_out_9), .out_10(part_3_out_10), .out_11(part_3_out_11), .out_12(part_3_out_12),
    .out_13(part_3_out_13), .out_14(part_3_out_14), .out_15(part_3_out_15), .out_16(part_3_out_16));
  or or_2 (or_2_out, part_1_out_10, blocker_for_bitshifter_4_out_12);
  or or_3 (or_3_out, part_1_out_11, blocker_for_bitshifter_4_out_13);
  or or_4 (or_4_out, part_3_out_11, blocker_for_bitshifter_5_out_13);
  or or_5 (or_5_out, part_3_out_9, blocker_for_bitshifter_5_out_11);
  or or_6 (or_6_out, part_3_out_10, blocker_for_bitshifter_5_out_12);
  circuit_2 part_4 (
    .in_1(blocker_for_bitshifter_3_out_11), .in_2(blocker_for_bitshifter_3_out_12),
    .in_3(blocker_for_bitshifter_3_out_13), .in_4(blocker_for_bitshifter_3_out_14),
    .in_5(blocker_for_bitshifter_3_out_15), .in_6(blocker_for_bitshifter_3_out_16),
    .in_7(blocker_for_bitshifter_3_out_17), .in_8(blocker_for_bitshifter_3_out_18), .out_9(part_4_out_9),
    .out_10(part_4_out_10), .out_11(part_4_out_11), .out_12(part_4_out_12), .out_13(part_4_out_13),
    .out_14(part_4_out_14), .out_15(part_4_out_15), .out_16(part_4_out_16));
  circuit_2 part_5 (
    .in_1(part_4_out_9), .in_2(part_4_out_10), .in_3(part_4_out_11), .in_4(part_4_out_12),
    .in_5(part_4_out_13), .in_6(part_4_out_14), .in_7(part_4_out_15), .in_8(part_4_out_16),
    .out_9(part_5_out_9), .out_10(part_5_out_10), .out_11(part_5_out_11), .out_12(part_5_out_12),
    .out_13(part_5_out_13), .out_14(part_5_out_14), .out_15(part_5_out_15), .out_16(part_5_out_16));
  circuit_2 part_6 (
    .in_1(part_5_out_9), .in_2(part_5_out_10), .in_3(part_5_out_11), .in_4(part_5_out_12),
    .in_5(part_5_out_13), .in_6(part_5_out_14), .in_7(part_5_out_15), .in_8(part_5_out_16),
    .out_9(part_6_out_9), .out_10(part_6_out_10), .out_11(part_6_out_11), .out_12(part_6_out_12),
    .out_13(part_6_out_13), .out_14(part_6_out_14), .out_15(part_6_out_15), .out_16(part_6_out_16));
  circuit_2 part_7 (
    .in_1(part_6_out_9), .in_2(part_6_out_10), .in_3(part_6_out_11), .in_4(part_6_out_12),
    .in_5(part_6_out_13), .in_6(part_6_out_14), .in_7(part_6_out_15), .in_8(part_6_out_16),
    .out_9(part_7_out_9), .out_10(part_7_out_10), .out_11(part_7_out_11), .out_12(part_7_out_12),
    .out_13(part_7_out_13), .out_14(part_7_out_14), .out_15(part_7_out_15), .out_16(part_7_out_16));
  or or_7 (out_12, part_7_out_9, blocker_for_bitshifter_6_out_11);
  or or_8 (out_13, part_7_out_10, blocker_for_bitshifter_6_out_12);
  or or_9 (out_14, part_7_out_11, blocker_for_bitshifter_6_out_13);
  or or_10 (or_10_out, part_1_out_12, blocker_for_bitshifter_4_out_14);
  or or_11 (or_11_out, part_1_out_13, blocker_for_bitshifter_4_out_15);
  or or_12 (or_12_out, part_1_out_14, blocker_for_bitshifter_4_out_16);
  or or_13 (or_13_out, part_3_out_14, blocker_for_bitshifter_5_out_16);
  or or_14 (or_14_out, part_3_out_12, blocker_for_bitshifter_5_out_14);
  or or_15 (or_15_out, part_3_out_13, blocker_for_bitshifter_5_out_15);
  or or_16 (out_16, part_7_out_13, blocker_for_bitshifter_6_out_15);
  or or_17 (out_15, part_7_out_12, blocker_for_bitshifter_6_out_14);
  blocker_for_bitshifter blocker_for_bitshifter_1 (
    .in_9(in_9), .out_10(blocker_for_bitshifter_1_out_10), .in_1(in_1), .in_2(in_2), .in_3(in_3),
    .in_4(in_4), .in_5(in_5), .in_6(in_6), .in_7(in_7), .in_8(in_8),
    .out_11(blocker_for_bitshifter_1_out_11), .out_12(blocker_for_bitshifter_1_out_12),
    .out_13(blocker_for_bitshifter_1_out_13), .out_14(blocker_for_bitshifter_1_out_14),
    .out_15(blocker_for_bitshifter_1_out_15), .out_16(blocker_for_bitshifter_1_out_16),
    .out_17(blocker_for_bitshifter_1_out_17), .out_18(blocker_for_bitshifter_1_out_18));
  or or_18 (or_18_out, part_1_out_16, blocker_for_bitshifter_4_out_18);
  or or_19 (or_19_out, part_1_out_15, blocker_for_bitshifter_4_out_17);
  blocker_for_bitshifter blocker_for_bitshifter_2 (
    .in_9(in_10), .out_10(blocker_for_bitshifter_2_out_10), .in_1(or_1_out), .in_2(or_2_out),
    .in_3(or_3_out), .in_4(or_10_out), .in_5(or_11_out), .in_6(or_12_out), .in_7(or_19_out),
    .in_8(or_18_out), .out_11(blocker_for_bitshifter_2_out_11), .out_12(blocker_for_bitshifter_2_out_12),
    .out_13(blocker_for_bitshifter_2_out_13), .out_14(blocker_for_bitshifter_2_out_14),
    .out_15(blocker_for_bitshifter_2_out_15), .out_16(blocker_for_bitshifter_2_out_16),
    .out_17(blocker_for_bitshifter_2_out_17), .out_18(blocker_for_bitshifter_2_out_18));
  or or_20 (or_20_out, part_3_out_16, blocker_for_bitshifter_5_out_18);
  or or_21 (or_21_out, part_3_out_15, blocker_for_bitshifter_5_out_17);
  blocker_for_bitshifter blocker_for_bitshifter_3 (
    .in_9(in_11), .out_10(blocker_for_bitshifter_3_out_10), .in_1(or_5_out), .in_2(or_6_out),
    .in_3(or_4_out), .in_4(or_14_out), .in_5(or_15_out), .in_6(or_13_out), .in_7(or_21_out),
    .in_8(or_20_out), .out_11(blocker_for_bitshifter_3_out_11), .out_12(blocker_for_bitshifter_3_out_12),
    .out_13(blocker_for_bitshifter_3_out_13), .out_14(blocker_for_bitshifter_3_out_14),
    .out_15(blocker_for_bitshifter_3_out_15), .out_16(blocker_for_bitshifter_3_out_16),
    .out_17(blocker_for_bitshifter_3_out_17), .out_18(blocker_for_bitshifter_3_out_18));
  or or_22 (out_17, part_7_out_14, blocker_for_bitshifter_6_out_16);
  or or_23 (out_18, part_7_out_15, blocker_for_bitshifter_6_out_17);
  or or_24 (out_19, part_7_out_16, blocker_for_bitshifter_6_out_18);
  blocker_for_bitshifter blocker_for_bitshifter_4 (
    .in_9(blocker_for_bitshifter_1_out_10), .in_1(in_1), .in_2(in_2), .in_3(in_3), .in_4(in_4), .in_5(in_5),
    .in_6(in_6), .in_7(in_7), .in_8(in_8), .out_11(blocker_for_bitshifter_4_out_11),
    .out_12(blocker_for_bitshifter_4_out_12), .out_13(blocker_for_bitshifter_4_out_13),
    .out_14(blocker_for_bitshifter_4_out_14), .out_15(blocker_for_bitshifter_4_out_15),
    .out_16(blocker_for_bitshifter_4_out_16), .out_17(blocker_for_bitshifter_4_out_17),
    .out_18(blocker_for_bitshifter_4_out_18));  // open: out_10
  blocker_for_bitshifter blocker_for_bitshifter_5 (
    .in_9(blocker_for_bitshifter_2_out_10), .in_1(or_1_out), .in_2(or_2_out), .in_3(or_3_out),
    .in_4(or_10_out), .in_5(or_11_out), .in_6(or_12_out), .in_7(or_19_out), .in_8(or_18_out),
    .out_11(blocker_for_bitshifter_5_out_11), .out_12(blocker_for_bitshifter_5_out_12),
    .out_13(blocker_for_bitshifter_5_out_13), .out_14(blocker_for_bitshifter_5_out_14),
    .out_15(blocker_for_bitshifter_5_out_15), .out_16(blocker_for_bitshifter_5_out_16),
    .out_17(blocker_for_bitshifter_5_out_17), .out_18(blocker_for_bitshifter_5_out_18));  // open: out_10
  blocker_for_bitshifter blocker_for_bitshifter_6 (
    .in_9(blocker_for_bitshifter_3_out_10), .in_1(or_5_out), .in_2(or_6_out), .in_3(or_4_out),
    .in_4(or_14_out), .in_5(or_15_out), .in_6(or_13_out), .in_7(or_21_out), .in_8(or_20_out),
    .out_11(blocker_for_bitshifter_6_out_11), .out_12(blocker_for_bitshifter_6_out_12),
    .out_13(blocker_for_bitshifter_6_out_13), .out_14(blocker_for_bitshifter_6_out_14),
    .out_15(blocker_for_bitshifter_6_out_15), .out_16(blocker_for_bitshifter_6_out_16),
    .out_17(blocker_for_bitshifter_6_out_17), .out_18(blocker_for_bitshifter_6_out_18));  // open: out_10
endmodule

module circuit_2 (
  input  in_1,
  input  in_2,
  input  in_3,
  input  in_4,
  input  in_5,
  input  in_6,
  input  in_7,
  input  in_8,
  output out_9,
  output out_10,
  output out_11,
  output out_12,
  output out_13,
  output out_14,
  output out_15,
  output out_16
);


  assign out_9 = 1'b0;
  assign out_10 = in_1;
  assign out_11 = in_2;
  assign out_12 = in_3;
  assign out_13 = in_4;
  assign out_14 = in_5;
  assign out_15 = in_6;
  assign out_16 = in_7;
endmodule

module bit_shifter_2 (
  input  in_1,
  input  in_2,
  input  in_3,
  input  in_4,
  input  in_5,
  input  in_6,
  input  in_7,
  input  in_8,
  input  in_9,
  input  in_10,
  input  in_11,
  output out_12,
  output out_13,
  output out_14,
  output out_15,
  output out_16,
  output out_17,
  output out_18,
  output out_19
);

  wire blocker_for_bitshifter_1_out_10, blocker_for_bitshifter_1_out_11, blocker_for_bitshifter_1_out_12,
       blocker_for_bitshifter_1_out_13, blocker_for_bitshifter_1_out_14, blocker_for_bitshifter_1_out_15,
       blocker_for_bitshifter_1_out_16, blocker_for_bitshifter_1_out_17, blocker_for_bitshifter_1_out_18,
       blocker_for_bitshifter_2_out_10, blocker_for_bitshifter_2_out_11, blocker_for_bitshifter_2_out_12,
       blocker_for_bitshifter_2_out_13, blocker_for_bitshifter_2_out_14, blocker_for_bitshifter_2_out_15,
       blocker_for_bitshifter_2_out_16, blocker_for_bitshifter_2_out_17, blocker_for_bitshifter_2_out_18,
       blocker_for_bitshifter_3_out_10, blocker_for_bitshifter_3_out_11, blocker_for_bitshifter_3_out_12,
       blocker_for_bitshifter_3_out_13, blocker_for_bitshifter_3_out_14, blocker_for_bitshifter_3_out_15,
       blocker_for_bitshifter_3_out_16, blocker_for_bitshifter_3_out_17, blocker_for_bitshifter_3_out_18,
       blocker_for_bitshifter_4_out_11, blocker_for_bitshifter_4_out_12, blocker_for_bitshifter_4_out_13,
       blocker_for_bitshifter_4_out_14, blocker_for_bitshifter_4_out_15, blocker_for_bitshifter_4_out_16,
       blocker_for_bitshifter_4_out_17, blocker_for_bitshifter_4_out_18, blocker_for_bitshifter_5_out_11,
       blocker_for_bitshifter_5_out_12, blocker_for_bitshifter_5_out_13, blocker_for_bitshifter_5_out_14,
       blocker_for_bitshifter_5_out_15, blocker_for_bitshifter_5_out_16, blocker_for_bitshifter_5_out_17,
       blocker_for_bitshifter_5_out_18, blocker_for_bitshifter_6_out_11, blocker_for_bitshifter_6_out_12,
       blocker_for_bitshifter_6_out_13, blocker_for_bitshifter_6_out_14, blocker_for_bitshifter_6_out_15,
       blocker_for_bitshifter_6_out_16, blocker_for_bitshifter_6_out_17, blocker_for_bitshifter_6_out_18,
       or_1_out, or_2_out, or_3_out, or_4_out, or_5_out, or_6_out, or_10_out, or_11_out, or_12_out,
       or_13_out, or_14_out, or_15_out, or_18_out, or_19_out, or_20_out, or_21_out, part_1_out_9,
       part_1_out_10, part_1_out_11, part_1_out_12, part_1_out_13, part_1_out_14, part_1_out_15,
       part_1_out_16, part_2_out_9, part_2_out_10, part_2_out_11, part_2_out_12, part_2_out_13,
       part_2_out_14, part_2_out_15, part_2_out_16, part_3_out_9, part_3_out_10, part_3_out_11,
       part_3_out_12, part_3_out_13, part_3_out_14, part_3_out_15, part_3_out_16, part_4_out_9,
       part_4_out_10, part_4_out_11, part_4_out_12, part_4_out_13, part_4_out_14, part_4_out_15,
       part_4_out_16, part_5_out_9, part_5_out_10, part_5_out_11, part_5_out_12, part_5_out_13,
       part_5_out_14, part_5_out_15, part_5_out_16, part_6_out_9, part_6_out_10, part_6_out_11,
       part_6_out_12, part_6_out_13, part_6_out_14, part_6_out_15, part_6_out_16, part_7_out_9,
       part_7_out_10, part_7_out_11, part_7_out_12, part_7_out_13, part_7_out_14, part_7_out_15,
       part_7_out_16;

  circuit_2_2 part_1 (
    .in_1(blocker_for_bitshifter_1_out_11), .in_2(blocker_for_bitshifter_1_out_12),
    .in_3(blocker_for_bitshifter_1_out_13), .in_4(blocker_for_bitshifter_1_out_14),
    .in_5(blocker_for_bitshifter_1_out_15), .in_6(blocker_for_bitshifter_1_out_16),
    .in_7(blocker_for_bitshifter_1_out_17), .in_8(blocker_for_bitshifter_1_out_18), .out_9(part_1_out_9),
    .out_10(part_1_out_10), .out_11(part_1_out_11), .out_12(part_1_out_12), .out_13(part_1_out_13),
    .out_14(part_1_out_14), .out_15(part_1_out_15), .out_16(part_1_out_16));
  or or_1 (or_1_out, part_1_out_9, blocker_for_bitshifter_4_out_11);
  circuit_2_2 part_2 (
    .in_1(blocker_for_bitshifter_2_out_11), .in_2(blocker_for_bitshifter_2_out_12),
    .in_3(blocker_for_bitshifter_2_out_13), .in_4(blocker_for_bitshifter_2_out_14),
    .in_5(blocker_for_bitshifter_2_out_15), .in_6(blocker_for_bitshifter_2_out_16),
    .in_7(blocker_for_bitshifter_2_out_17), .in_8(blocker_for_bitshifter_2_out_18), .out_9(part_2_out_9),
    .out_10(part_2_out_10), .out_11(part_2_out_11), .out_12(part_2_out_12), .out_13(part_2_out_13),
    .out_14(part_2_out_14), .out_15(part_2_out_15), .out_16(part_2_out_16));
  circuit_2_2 part_3 (
    .in_1(part_2_out_9), .in_2(part_2_out_10), .in_3(part_2_out_11), .in_4(part_2_out_12),
    .in_5(part_2_out_13), .in_6(part_2_out_14), .in_7(part_2_out_15), .in_8(part_2_out_16),
    .out_9(part_3_out_9), .out_10(part_3_out_10), .out_11(part_3_out_11), .out_12(part_3_out_12),
    .out_13(part_3_out_13), .out_14(part_3_out_14), .out_15(part_3_out_15), .out_16(part_3_out_16));
  or or_2 (or_2_out, part_1_out_11, blocker_for_bitshifter_4_out_13);
  or or_3 (or_3_out, part_1_out_10, blocker_for_bitshifter_4_out_12);
  or or_4 (or_4_out, part_3_out_9, blocker_for_bitshifter_5_out_11);
  or or_5 (or_5_out, part_3_out_10, blocker_for_bitshifter_5_out_12);
  or or_6 (or_6_out, part_3_out_11, blocker_for_bitshifter_5_out_13);
  circuit_2_2 part_4 (
    .in_1(blocker_for_bitshifter_3_out_11), .in_2(blocker_for_bitshifter_3_out_12),
    .in_3(blocker_for_bitshifter_3_out_13), .in_4(blocker_for_bitshifter_3_out_14),
    .in_5(blocker_for_bitshifter_3_out_15), .in_6(blocker_for_bitshifter_3_out_16),
    .in_7(blocker_for_bitshifter_3_out_17), .in_8(blocker_for_bitshifter_3_out_18), .out_9(part_4_out_9),
    .out_10(part_4_out_10), .out_11(part_4_out_11), .out_12(part_4_out_12), .out_13(part_4_out_13),
    .out_14(part_4_out_14), .out_15(part_4_out_15), .out_16(part_4_out_16));
  circuit_2_2 part_5 (
    .in_1(part_4_out_9), .in_2(part_4_out_10), .in_3(part_4_out_11), .in_4(part_4_out_12),
    .in_5(part_4_out_13), .in_6(part_4_out_14), .in_7(part_4_out_15), .in_8(part_4_out_16),
    .out_9(part_5_out_9), .out_10(part_5_out_10), .out_11(part_5_out_11), .out_12(part_5_out_12),
    .out_13(part_5_out_13), .out_14(part_5_out_14), .out_15(part_5_out_15), .out_16(part_5_out_16));
  circuit_2_2 part_6 (
    .in_1(part_5_out_9), .in_2(part_5_out_10), .in_3(part_5_out_11), .in_4(part_5_out_12),
    .in_5(part_5_out_13), .in_6(part_5_out_14), .in_7(part_5_out_15), .in_8(part_5_out_16),
    .out_9(part_6_out_9), .out_10(part_6_out_10), .out_11(part_6_out_11), .out_12(part_6_out_12),
    .out_13(part_6_out_13), .out_14(part_6_out_14), .out_15(part_6_out_15), .out_16(part_6_out_16));
  circuit_2_2 part_7 (
    .in_1(part_6_out_9), .in_2(part_6_out_10), .in_3(part_6_out_11), .in_4(part_6_out_12),
    .in_5(part_6_out_13), .in_6(part_6_out_14), .in_7(part_6_out_15), .in_8(part_6_out_16),
    .out_9(part_7_out_9), .out_10(part_7_out_10), .out_11(part_7_out_11), .out_12(part_7_out_12),
    .out_13(part_7_out_13), .out_14(part_7_out_14), .out_15(part_7_out_15), .out_16(part_7_out_16));
  or or_7 (out_12, part_7_out_9, blocker_for_bitshifter_6_out_11);
  or or_8 (out_13, part_7_out_10, blocker_for_bitshifter_6_out_12);
  or or_9 (out_14, part_7_out_11, blocker_for_bitshifter_6_out_13);
  or or_10 (or_10_out, part_1_out_13, blocker_for_bitshifter_4_out_15);
  or or_11 (or_11_out, part_1_out_12, blocker_for_bitshifter_4_out_14);
  or or_12 (or_12_out, part_1_out_14, blocker_for_bitshifter_4_out_16);
  or or_13 (or_13_out, part_3_out_13, blocker_for_bitshifter_5_out_15);
  or or_14 (or_14_out, part_3_out_14, blocker_for_bitshifter_5_out_16);
  or or_15 (or_15_out, part_3_out_12, blocker_for_bitshifter_5_out_14);
  or or_16 (out_15, part_7_out_12, blocker_for_bitshifter_6_out_14);
  or or_17 (out_16, part_7_out_13, blocker_for_bitshifter_6_out_15);
  blocker_for_bitshifter blocker_for_bitshifter_1 (
    .in_9(in_9), .out_10(blocker_for_bitshifter_1_out_10), .in_1(in_1), .in_2(in_2), .in_3(in_3),
    .in_4(in_4), .in_5(in_5), .in_6(in_6), .in_7(in_7), .in_8(in_8),
    .out_11(blocker_for_bitshifter_1_out_11), .out_12(blocker_for_bitshifter_1_out_12),
    .out_13(blocker_for_bitshifter_1_out_13), .out_14(blocker_for_bitshifter_1_out_14),
    .out_15(blocker_for_bitshifter_1_out_15), .out_16(blocker_for_bitshifter_1_out_16),
    .out_17(blocker_for_bitshifter_1_out_17), .out_18(blocker_for_bitshifter_1_out_18));
  or or_18 (or_18_out, part_1_out_15, blocker_for_bitshifter_4_out_17);
  or or_19 (or_19_out, part_1_out_16, blocker_for_bitshifter_4_out_18);
  blocker_for_bitshifter blocker_for_bitshifter_2 (
    .in_9(in_10), .out_10(blocker_for_bitshifter_2_out_10), .in_1(or_1_out), .in_2(or_3_out),
    .in_3(or_2_out), .in_4(or_11_out), .in_5(or_10_out), .in_6(or_12_out), .in_7(or_18_out),
    .in_8(or_19_out), .out_11(blocker_for_bitshifter_2_out_11), .out_12(blocker_for_bitshifter_2_out_12),
    .out_13(blocker_for_bitshifter_2_out_13), .out_14(blocker_for_bitshifter_2_out_14),
    .out_15(blocker_for_bitshifter_2_out_15), .out_16(blocker_for_bitshifter_2_out_16),
    .out_17(blocker_for_bitshifter_2_out_17), .out_18(blocker_for_bitshifter_2_out_18));
  or or_20 (or_20_out, part_3_out_16, blocker_for_bitshifter_5_out_18);
  or or_21 (or_21_out, part_3_out_15, blocker_for_bitshifter_5_out_17);
  blocker_for_bitshifter blocker_for_bitshifter_3 (
    .in_9(in_11), .out_10(blocker_for_bitshifter_3_out_10), .in_1(or_4_out), .in_2(or_5_out),
    .in_3(or_6_out), .in_4(or_15_out), .in_5(or_13_out), .in_6(or_14_out), .in_7(or_21_out),
    .in_8(or_20_out), .out_11(blocker_for_bitshifter_3_out_11), .out_12(blocker_for_bitshifter_3_out_12),
    .out_13(blocker_for_bitshifter_3_out_13), .out_14(blocker_for_bitshifter_3_out_14),
    .out_15(blocker_for_bitshifter_3_out_15), .out_16(blocker_for_bitshifter_3_out_16),
    .out_17(blocker_for_bitshifter_3_out_17), .out_18(blocker_for_bitshifter_3_out_18));
  or or_22 (out_19, part_7_out_16, blocker_for_bitshifter_6_out_18);
  or or_23 (out_18, part_7_out_15, blocker_for_bitshifter_6_out_17);
  or or_24 (out_17, part_7_out_14, blocker_for_bitshifter_6_out_16);
  blocker_for_bitshifter blocker_for_bitshifter_4 (
    .in_9(blocker_for_bitshifter_1_out_10), .in_1(in_1), .in_2(in_2), .in_3(in_3), .in_4(in_4), .in_5(in_5),
    .in_6(in_6), .in_7(in_7), .in_8(in_8), .out_11(blocker_for_bitshifter_4_out_11),
    .out_12(blocker_for_bitshifter_4_out_12), .out_13(blocker_for_bitshifter_4_out_13),
    .out_14(blocker_for_bitshifter_4_out_14), .out_15(blocker_for_bitshifter_4_out_15),
    .out_16(blocker_for_bitshifter_4_out_16), .out_17(blocker_for_bitshifter_4_out_17),
    .out_18(blocker_for_bitshifter_4_out_18));  // open: out_10
  blocker_for_bitshifter blocker_for_bitshifter_5 (
    .in_9(blocker_for_bitshifter_2_out_10), .in_1(or_1_out), .in_2(or_3_out), .in_3(or_2_out),
    .in_4(or_11_out), .in_5(or_10_out), .in_6(or_12_out), .in_7(or_18_out), .in_8(or_19_out),
    .out_11(blocker_for_bitshifter_5_out_11), .out_12(blocker_for_bitshifter_5_out_12),
    .out_13(blocker_for_bitshifter_5_out_13), .out_14(blocker_for_bitshifter_5_out_14),
    .out_15(blocker_for_bitshifter_5_out_15), .out_16(blocker_for_bitshifter_5_out_16),
    .out_17(blocker_for_bitshifter_5_out_17), .out_18(blocker_for_bitshifter_5_out_18));  // open: out_10
  blocker_for_bitshifter blocker_for_bitshifter_6 (
    .in_9(blocker_for_bitshifter_3_out_10), .in_1(or_4_out), .in_2(or_5_out), .in_3(or_6_out),
    .in_4(or_15_out), .in_5(or_13_out), .in_6(or_14_out), .in_7(or_21_out), .in_8(or_20_out),
    .out_11(blocker_for_bitshifter_6_out_11), .out_12(blocker_for_bitshifter_6_out_12),
    .out_13(blocker_for_bitshifter_6_out_13), .out_14(blocker_for_bitshifter_6_out_14),
    .out_15(blocker_for_bitshifter_6_out_15), .out_16(blocker_for_bitshifter_6_out_16),
    .out_17(blocker_for_bitshifter_6_out_17), .out_18(blocker_for_bitshifter_6_out_18));  // open: out_10
endmodule

module circuit_2_2 (
  input  in_1,
  input  in_2,
  input  in_3,
  input  in_4,
  input  in_5,
  input  in_6,
  input  in_7,
  input  in_8,
  output out_9,
  output out_10,
  output out_11,
  output out_12,
  output out_13,
  output out_14,
  output out_15,
  output out_16
);


  assign out_9 = in_2;
  assign out_10 = in_3;
  assign out_11 = in_4;
  assign out_12 = in_5;
  assign out_13 = in_6;
  assign out_14 = in_7;
  assign out_15 = in_8;
  assign out_16 = 1'b0;
endmodule

module ALU (
  input  A,
  input  in_2,
  input  in_3,
  input  in_4,
  input  in_5,
  input  in_6,
  input  in_7,
  input  in_8,
  input  B,
  input  in_10,
  input  in_11,
  input  in_12,
  input  in_13,
  input  in_14,
  input  in_15,
  input  in_16,
  input  in_17,
  input  in_18,
  input  in_19,
  input  in_20,
  input  CIN,
  output _1,
  output _2,
  output _4,
  output _8,
  output _16,
  output _32,
  output _64,
  output _128,
  output COUT,
  output ZERO_flag
);

  wire a_b_1_out_17, a_b_1_out_18, a_b_1_out_19, a_b_1_out_20, a_b_1_out_21, a_b_1_out_22, a_b_1_out_23,
       a_b_1_out_24, a_b_2_out_17, a_b_2_out_18, a_b_2_out_19, a_b_2_out_20, a_b_2_out_21, a_b_2_out_22,
       a_b_2_out_23, a_b_2_out_24, and_1_out, and_2_out, bit_shifter_1_out_12, bit_shifter_1_out_13,
       bit_shifter_1_out_14, bit_shifter_1_out_15, bit_shifter_1_out_16, bit_shifter_1_out_17,
       bit_shifter_1_out_18, bit_shifter_1_out_19, bit_shifter_2_out_12, bit_shifter_2_out_13,
       bit_shifter_2_out_14, bit_shifter_2_out_15, bit_shifter_2_out_16, bit_shifter_2_out_17,
       bit_shifter_2_out_18, bit_shifter_2_out_19, if_odd_1_out_9, mult_out_17, mult_out_18, mult_out_19,
       mult_out_20, mult_out_21, mult_out_22, mult_out_23, mult_out_24, n4_bit_multiplexer_1_out_5,
       n4_bit_multiplexer_1_out_6, n4_bit_multiplexer_1_out_7, n4_bit_multiplexer_1_out_8,
       n4_bit_multiplexer_1_out_9, n4_bit_multiplexer_1_out_10, n4_bit_multiplexer_1_out_11,
       n4_bit_multiplexer_1_out_12, n4_bit_multiplexer_1_out_13, n4_bit_multiplexer_1_out_14,
       n4_bit_multiplexer_1_out_15, n4_bit_multiplexer_1_out_16, n4_bit_multiplexer_1_out_17,
       n4_bit_multiplexer_1_out_18, n4_bit_multiplexer_1_out_19, n4_bit_multiplexer_1_out_20,
       n8_bit_adder_1_cout, n8_bit_adder_1_out_18, n8_bit_adder_1_out_19, n8_bit_adder_1_out_20,
       n8_bit_adder_1_out_21, n8_bit_adder_1_out_22, n8_bit_adder_1_out_23, n8_bit_adder_1_out_24,
       n8_bit_adder_1_out_25, n8_bit_blocker_alu_1_out_18, n8_bit_blocker_alu_1_out_19,
       n8_bit_blocker_alu_1_out_20, n8_bit_blocker_alu_1_out_21, n8_bit_blocker_alu_1_out_22,
       n8_bit_blocker_alu_1_out_23, n8_bit_blocker_alu_1_out_24, n8_bit_blocker_alu_1_out_25,
       n8_bit_blocker_alu_1_out_26, n8_bit_blocker_alu_1_out_27, n8_bit_blocker_alu_1_out_28,
       n8_bit_blocker_alu_1_out_29, n8_bit_blocker_alu_1_out_30, n8_bit_blocker_alu_1_out_31,
       n8_bit_blocker_alu_1_out_32, n8_bit_blocker_alu_1_out_33, n8_bit_blocker_alu_2_out_18,
       n8_bit_blocker_alu_2_out_19, n8_bit_blocker_alu_2_out_20, n8_bit_blocker_alu_2_out_21,
       n8_bit_blocker_alu_2_out_22, n8_bit_blocker_alu_2_out_23, n8_bit_blocker_alu_2_out_24,
       n8_bit_blocker_alu_2_out_25, n8_bit_blocker_alu_2_out_26, n8_bit_blocker_alu_2_out_27,
       n8_bit_blocker_alu_2_out_28, n8_bit_blocker_alu_2_out_29, n8_bit_blocker_alu_2_out_30,
       n8_bit_blocker_alu_2_out_31, n8_bit_blocker_alu_2_out_32, n8_bit_blocker_alu_2_out_33,
       n8_bit_blocker_alu_3_out_18, n8_bit_blocker_alu_3_out_19, n8_bit_blocker_alu_3_out_20,
       n8_bit_blocker_alu_3_out_21, n8_bit_blocker_alu_3_out_22, n8_bit_blocker_alu_3_out_23,
       n8_bit_blocker_alu_3_out_24, n8_bit_blocker_alu_3_out_25, n8_bit_blocker_alu_3_out_26,
       n8_bit_blocker_alu_3_out_27, n8_bit_blocker_alu_3_out_28, n8_bit_blocker_alu_3_out_29,
       n8_bit_blocker_alu_3_out_30, n8_bit_blocker_alu_3_out_31, n8_bit_blocker_alu_3_out_32,
       n8_bit_blocker_alu_3_out_33, n8_bit_blocker_alu_4_out_18, n8_bit_blocker_alu_4_out_19,
       n8_bit_blocker_alu_4_out_20, n8_bit_blocker_alu_4_out_21, n8_bit_blocker_alu_4_out_22,
       n8_bit_blocker_alu_4_out_23, n8_bit_blocker_alu_4_out_24, n8_bit_blocker_alu_4_out_25,
       n8_bit_blocker_alu_4_out_26, n8_bit_blocker_alu_4_out_27, n8_bit_blocker_alu_4_out_28,
       n8_bit_blocker_alu_4_out_29, n8_bit_blocker_alu_4_out_30, n8_bit_blocker_alu_4_out_31,
       n8_bit_blocker_alu_4_out_32, n8_bit_blocker_alu_4_out_33, n8_bit_blocker_alu_5_out_18,
       n8_bit_blocker_alu_5_out_19, n8_bit_blocker_alu_5_out_20, n8_bit_blocker_alu_5_out_21,
       n8_bit_blocker_alu_5_out_22, n8_bit_blocker_alu_5_out_23, n8_bit_blocker_alu_5_out_24,
       n8_bit_blocker_alu_5_out_25, n8_bit_blocker_alu_5_out_26, n8_bit_blocker_alu_5_out_27,
       n8_bit_blocker_alu_5_out_28, n8_bit_blocker_alu_5_out_29, n8_bit_blocker_alu_5_out_30,
       n8_bit_blocker_alu_5_out_31, n8_bit_blocker_alu_5_out_32, n8_bit_blocker_alu_5_out_33,
       n8_bit_blocker_alu_6_out_18, n8_bit_blocker_alu_6_out_19, n8_bit_blocker_alu_6_out_20,
       n8_bit_blocker_alu_6_out_21, n8_bit_blocker_alu_6_out_22, n8_bit_blocker_alu_6_out_23,
       n8_bit_blocker_alu_6_out_24, n8_bit_blocker_alu_6_out_25, n8_bit_blocker_alu_7_out_26,
       n8_bit_blocker_alu_7_out_27, n8_bit_blocker_alu_7_out_28, n8_bit_blocker_alu_7_out_29,
       n8_bit_blocker_alu_7_out_30, n8_bit_blocker_alu_7_out_31, n8_bit_blocker_alu_7_out_32,
       n8_bit_blocker_alu_7_out_33, n8_bit_blocker_alu_8_out_18, n8_bit_blocker_alu_8_out_19,
       n8_bit_blocker_alu_8_out_20, n8_bit_blocker_alu_8_out_21, n8_bit_blocker_alu_8_out_22,
       n8_bit_blocker_alu_8_out_23, n8_bit_blocker_alu_8_out_24, n8_bit_blocker_alu_8_out_25,
       n8_bit_blocker_alu_8_out_26, n8_bit_blocker_alu_8_out_27, n8_bit_blocker_alu_8_out_28,
       n8_bit_blocker_alu_9_out_18, n8_bit_blocker_alu_9_out_19, n8_bit_blocker_alu_9_out_20,
       n8_bit_blocker_alu_9_out_21, n8_bit_blocker_alu_9_out_22, n8_bit_blocker_alu_9_out_23,
       n8_bit_blocker_alu_9_out_24, n8_bit_blocker_alu_9_out_25, n8_bit_blocker_alu_9_out_26,
       n8_bit_blocker_alu_9_out_27, n8_bit_blocker_alu_9_out_28, n8_bit_blocker_alu_10_out_18,
       n8_bit_blocker_alu_10_out_19, n8_bit_blocker_alu_10_out_20, n8_bit_blocker_alu_10_out_21,
       n8_bit_blocker_alu_10_out_22, n8_bit_blocker_alu_10_out_23, n8_bit_blocker_alu_10_out_24,
       n8_bit_blocker_alu_10_out_25, n8_bit_blocker_alu_10_out_26, n8_bit_blocker_alu_10_out_27,
       n8_bit_blocker_alu_10_out_28, n8_bit_blocker_alu_10_out_29, n8_bit_blocker_alu_10_out_30,
       n8_bit_blocker_alu_10_out_31, n8_bit_blocker_alu_10_out_32, n8_bit_blocker_alu_10_out_33,
       n8_bit_blocker_alu_11_out_18, n8_bit_blocker_alu_11_out_19, n8_bit_blocker_alu_11_out_20,
       n8_bit_blocker_alu_11_out_21, n8_bit_blocker_alu_11_out_22, n8_bit_blocker_alu_11_out_23,
       n8_bit_blocker_alu_11_out_24, n8_bit_blocker_alu_11_out_25, n8_bit_blocker_alu_11_out_26,
       n8_bit_blocker_alu_11_out_27, n8_bit_blocker_alu_11_out_28, n8_bit_blocker_alu_11_out_29,
       n8_bit_blocker_alu_11_out_30, n8_bit_blocker_alu_11_out_31, n8_bit_blocker_alu_11_out_32,
       n8_bit_blocker_alu_11_out_33, n8_bit_blocker_alu_12_out_18, n8_bit_blocker_alu_12_out_19,
       n8_bit_blocker_alu_12_out_20, n8_bit_blocker_alu_12_out_21, n8_bit_blocker_alu_12_out_22,
       n8_bit_blocker_alu_12_out_23, n8_bit_blocker_alu_12_out_24, n8_bit_blocker_alu_12_out_25,
       n8_bit_subtractor_1_out_18, n8_bit_subtractor_1_out_19, n8_bit_subtractor_1_out_20,
       n8_bit_subtractor_1_out_21, n8_bit_subtractor_1_out_22, n8_bit_subtractor_1_out_23,
       n8_bit_subtractor_1_out_24, n8_bit_subtractor_1_out_25, n8_bit_subtractor_1_out_26, not_1_out,
       not_2_out, not_3_out, not_4_out, or_1_out, or_11_out, or_12_out, or_13_out, or_14_out, or_15_out,
       or_16_out, or_17_out, or_18_out, or_19_out, or_20_out, or_21_out, or_22_out, or_23_out, or_24_out,
       or_25_out, or_26_out, or_27_out, or_28_out, or_29_out, or_30_out, or_31_out, or_32_out, or_33_out,
       or_34_out, or_35_out, or_36_out, or_37_out, or_38_out, or_39_out, or_40_out, or_41_out, or_42_out,
       or_43_out, or_44_out, or_45_out, or_46_out, or_47_out, or_48_out, or_49_out, or_50_out, or_51_out,
       or_52_out, or_53_out, or_54_out, or_55_out, or_56_out, or_57_out, or_58_out, or_59_out, or_60_out,
       or_61_out, or_62_out, or_63_out, or_64_out, or_65_out, or_66_out, or_67_out, or_68_out, or_69_out,
       or_70_out, or_71_out, or_72_out, or_73_out, or_74_out, or_75_out, or_76_out, or_77_out, or_78_out,
       or_79_out, or_80_out, or_81_out, or_82_out, or_83_out, or_84_out, or_85_out, or_86_out, part_1_out_9,
       part_1_out_10, part_1_out_11, part_1_out_12, part_1_out_13, part_1_out_14, part_1_out_15,
       part_1_out_16, part_2_out_9, part_2_out_10, part_2_out_11, part_2_out_12, part_2_out_13,
       part_2_out_14, part_2_out_15, part_2_out_16, strtopair_1_out_17, strtopair_1_out_18,
       strtopair_1_out_19, strtopair_1_out_20, strtopair_1_out_21, strtopair_1_out_22, strtopair_1_out_23,
       strtopair_1_out_24, strtopair_1_out_25, strtopair_1_out_26, strtopair_1_out_27, strtopair_1_out_28,
       strtopair_1_out_29, strtopair_1_out_30, strtopair_1_out_31, strtopair_1_out_32, strtopair_2_out_17,
       strtopair_2_out_18, strtopair_2_out_19, strtopair_2_out_20, strtopair_2_out_21, strtopair_2_out_22,
       strtopair_2_out_23, strtopair_2_out_24, strtopair_2_out_25, strtopair_2_out_26, strtopair_2_out_27,
       strtopair_2_out_28, strtopair_2_out_29, strtopair_2_out_30, strtopair_2_out_31, strtopair_2_out_32,
       strtopair_3_out_17, strtopair_3_out_18, strtopair_3_out_19, strtopair_3_out_20, strtopair_3_out_21,
       strtopair_3_out_22, strtopair_3_out_23, strtopair_3_out_24, strtopair_3_out_25, strtopair_3_out_26,
       strtopair_3_out_27, strtopair_3_out_28, strtopair_3_out_29, strtopair_3_out_30, strtopair_3_out_31,
       strtopair_3_out_32, strtopair_4_out_17, strtopair_4_out_18, strtopair_4_out_19, strtopair_4_out_20,
       strtopair_4_out_21, strtopair_4_out_22, strtopair_4_out_23, strtopair_4_out_24, strtopair_4_out_25,
       strtopair_4_out_26, strtopair_4_out_27, strtopair_4_out_28, strtopair_4_out_29, strtopair_4_out_30,
       strtopair_4_out_31, strtopair_4_out_32, strtopair_5_out_17, strtopair_5_out_18, strtopair_5_out_19,
       strtopair_5_out_20, strtopair_5_out_21, strtopair_5_out_22, strtopair_5_out_23, strtopair_5_out_24,
       strtopair_5_out_25, strtopair_5_out_26, strtopair_5_out_27, strtopair_5_out_28, strtopair_5_out_29,
       strtopair_5_out_30, strtopair_5_out_31, strtopair_5_out_32, strtopair_6_out_17, strtopair_6_out_18,
       strtopair_6_out_19, strtopair_6_out_20, strtopair_6_out_21, strtopair_6_out_22, strtopair_6_out_23,
       strtopair_6_out_24, strtopair_6_out_25, strtopair_6_out_26, strtopair_6_out_27, strtopair_6_out_28,
       strtopair_6_out_29, strtopair_6_out_30, strtopair_6_out_31, strtopair_6_out_32, XOR_out_17,
       XOR_out_18, XOR_out_19, XOR_out_20, XOR_out_21, XOR_out_22, XOR_out_23, XOR_out_24;

  or or_1 (or_1_out, n4_bit_multiplexer_1_out_19, n4_bit_multiplexer_1_out_6);
  _4_bit_multiplexer u_4_bit_multiplexer_1 (
    ._1(not_4_out), ._2(not_2_out), ._3(not_3_out), ._4(not_1_out), .out_5(n4_bit_multiplexer_1_out_5),
    .out_6(n4_bit_multiplexer_1_out_6), .out_7(n4_bit_multiplexer_1_out_7),
    .out_8(n4_bit_multiplexer_1_out_8), .out_9(n4_bit_multiplexer_1_out_9),
    .out_10(n4_bit_multiplexer_1_out_10), .out_11(n4_bit_multiplexer_1_out_11),
    .out_12(n4_bit_multiplexer_1_out_12), .out_13(n4_bit_multiplexer_1_out_13),
    .out_14(n4_bit_multiplexer_1_out_14), .out_15(n4_bit_multiplexer_1_out_15),
    .out_16(n4_bit_multiplexer_1_out_16), .out_17(n4_bit_multiplexer_1_out_17),
    .out_18(n4_bit_multiplexer_1_out_18), .out_19(n4_bit_multiplexer_1_out_19),
    .out_20(n4_bit_multiplexer_1_out_20));
  not not_1 (not_1_out, in_20);
  not not_2 (not_2_out, in_18);
  not not_3 (not_3_out, in_19);
  not not_4 (not_4_out, in_17);
  _8_bit_blocker_ALU u_8_bit_blocker_alu_1 (
    .in_9(or_1_out), .out_18(n8_bit_blocker_alu_1_out_18), .out_19(n8_bit_blocker_alu_1_out_19),
    .out_20(n8_bit_blocker_alu_1_out_20), .out_21(n8_bit_blocker_alu_1_out_21),
    .out_22(n8_bit_blocker_alu_1_out_22), .out_23(n8_bit_blocker_alu_1_out_23),
    .out_24(n8_bit_blocker_alu_1_out_24), .out_25(n8_bit_blocker_alu_1_out_25),
    .out_26(n8_bit_blocker_alu_1_out_26), .out_27(n8_bit_blocker_alu_1_out_27),
    .out_28(n8_bit_blocker_alu_1_out_28), .out_29(n8_bit_blocker_alu_1_out_29),
    .out_30(n8_bit_blocker_alu_1_out_30), .out_31(n8_bit_blocker_alu_1_out_31),
    .out_32(n8_bit_blocker_alu_1_out_32), .out_33(n8_bit_blocker_alu_1_out_33), .in_1(in_8), .in_2(in_7),
    .in_3(in_6), .in_4(in_5), .in_5(in_4), .in_6(in_3), .in_7(in_2), .in_8(A), .in_10(B), .in_11(in_10),
    .in_12(in_11), .in_13(in_12), .in_14(in_13), .in_15(in_14), .in_16(in_15), .in_17(in_16));
  or or_2 (_1, or_13_out, n8_bit_adder_1_out_18);
  or or_3 (_2, or_14_out, n8_bit_adder_1_out_19);
  or or_4 (_4, or_15_out, n8_bit_adder_1_out_20);
  or or_5 (_8, or_16_out, n8_bit_adder_1_out_21);
  or or_6 (_16, or_17_out, n8_bit_adder_1_out_22);
  or or_7 (_32, or_18_out, n8_bit_adder_1_out_23);
  or or_8 (_64, or_19_out, n8_bit_adder_1_out_24);
  or or_9 (_128, or_20_out, n8_bit_adder_1_out_25);
  or or_10 (COUT, n8_bit_subtractor_1_out_26, n8_bit_adder_1_cout);
  STRtoPAIR strtopair_1 (
    .in_1(n8_bit_blocker_alu_1_out_18), .in_2(n8_bit_blocker_alu_1_out_20),
    .in_3(n8_bit_blocker_alu_1_out_22), .in_4(n8_bit_blocker_alu_1_out_24),
    .in_5(n8_bit_blocker_alu_1_out_26), .in_6(n8_bit_blocker_alu_1_out_28),
    .in_7(n8_bit_blocker_alu_1_out_30), .in_8(n8_bit_blocker_alu_1_out_32),
    .in_9(n8_bit_blocker_alu_1_out_19), .in_10(n8_bit_blocker_alu_1_out_21),
    .in_11(n8_bit_blocker_alu_1_out_23), .in_12(n8_bit_blocker_alu_1_out_25),
    .in_13(n8_bit_blocker_alu_1_out_27), .in_14(n8_bit_blocker_alu_1_out_29),
    .in_15(n8_bit_blocker_alu_1_out_31), .in_16(n8_bit_blocker_alu_1_out_33), .out_17(strtopair_1_out_17),
    .out_18(strtopair_1_out_18), .out_19(strtopair_1_out_19), .out_20(strtopair_1_out_20),
    .out_21(strtopair_1_out_21), .out_22(strtopair_1_out_22), .out_23(strtopair_1_out_23),
    .out_24(strtopair_1_out_24), .out_25(strtopair_1_out_25), .out_26(strtopair_1_out_26),
    .out_27(strtopair_1_out_27), .out_28(strtopair_1_out_28), .out_29(strtopair_1_out_29),
    .out_30(strtopair_1_out_30), .out_31(strtopair_1_out_31), .out_32(strtopair_1_out_32));
  _8_bit_adder u_8_bit_adder_1 (
    .in_2(strtopair_1_out_17), ._1(strtopair_1_out_25), .in_4(strtopair_1_out_18), ._2(strtopair_1_out_26),
    .in_6(strtopair_1_out_19), ._4(strtopair_1_out_27), .in_8(strtopair_1_out_20), ._8(strtopair_1_out_28),
    .in_10(strtopair_1_out_21), ._16(strtopair_1_out_29), .in_12(strtopair_1_out_22),
    ._32(strtopair_1_out_30), .in_14(strtopair_1_out_23), ._64(strtopair_1_out_31),
    .in_16(strtopair_1_out_24), ._128(strtopair_1_out_32), .Cin(and_2_out), .Cout(n8_bit_adder_1_cout),
    .out_18(n8_bit_adder_1_out_18), .out_19(n8_bit_adder_1_out_19), .out_20(n8_bit_adder_1_out_20),
    .out_21(n8_bit_adder_1_out_21), .out_22(n8_bit_adder_1_out_22), .out_23(n8_bit_adder_1_out_23),
    .out_24(n8_bit_adder_1_out_24), .out_25(n8_bit_adder_1_out_25));
  and and_1 (and_1_out, or_11_out, or_12_out);
  and and_2 (and_2_out, or_1_out, or_11_out);
  or or_11 (or_11_out, CIN, n4_bit_multiplexer_1_out_20, n4_bit_multiplexer_1_out_19);
  or or_12 (or_12_out, n4_bit_multiplexer_1_out_7, n4_bit_multiplexer_1_out_20);
  _8_bit_blocker_ALU u_8_bit_blocker_alu_2 (
    .in_9(or_12_out), .out_18(n8_bit_blocker_alu_2_out_18), .out_19(n8_bit_blocker_alu_2_out_19),
    .out_20(n8_bit_blocker_alu_2_out_20), .out_21(n8_bit_blocker_alu_2_out_21),
    .out_22(n8_bit_blocker_alu_2_out_22), .out_23(n8_bit_blocker_alu_2_out_23),
    .out_24(n8_bit_blocker_alu_2_out_24), .out_25(n8_bit_blocker_alu_2_out_25),
    .out_26(n8_bit_blocker_alu_2_out_26), .out_27(n8_bit_blocker_alu_2_out_27),
    .out_28(n8_bit_blocker_alu_2_out_28), .out_29(n8_bit_blocker_alu_2_out_29),
    .out_30(n8_bit_blocker_alu_2_out_30), .out_31(n8_bit_blocker_alu_2_out_31),
    .out_32(n8_bit_blocker_alu_2_out_32), .out_33(n8_bit_blocker_alu_2_out_33), .in_1(in_8), .in_2(in_7),
    .in_3(in_6), .in_4(in_5), .in_5(in_4), .in_6(in_3), .in_7(in_2), .in_8(A), .in_10(B), .in_11(in_10),
    .in_12(in_11), .in_13(in_12), .in_14(in_13), .in_15(in_14), .in_16(in_15), .in_17(in_16));
  STRtoPAIR strtopair_2 (
    .in_1(n8_bit_blocker_alu_2_out_18), .in_2(n8_bit_blocker_alu_2_out_20),
    .in_3(n8_bit_blocker_alu_2_out_22), .in_4(n8_bit_blocker_alu_2_out_24),
    .in_5(n8_bit_blocker_alu_2_out_26), .in_6(n8_bit_blocker_alu_2_out_28),
    .in_7(n8_bit_blocker_alu_2_out_30), .in_8(n8_bit_blocker_alu_2_out_32),
    .in_9(n8_bit_blocker_alu_2_out_19), .in_10(n8_bit_blocker_alu_2_out_21),
    .in_11(n8_bit_blocker_alu_2_out_23), .in_12(n8_bit_blocker_alu_2_out_25),
    .in_13(n8_bit_blocker_alu_2_out_27), .in_14(n8_bit_blocker_alu_2_out_29),
    .in_15(n8_bit_blocker_alu_2_out_31), .in_16(n8_bit_blocker_alu_2_out_33), .out_17(strtopair_2_out_17),
    .out_18(strtopair_2_out_18), .out_19(strtopair_2_out_19), .out_20(strtopair_2_out_20),
    .out_21(strtopair_2_out_21), .out_22(strtopair_2_out_22), .out_23(strtopair_2_out_23),
    .out_24(strtopair_2_out_24), .out_25(strtopair_2_out_25), .out_26(strtopair_2_out_26),
    .out_27(strtopair_2_out_27), .out_28(strtopair_2_out_28), .out_29(strtopair_2_out_29),
    .out_30(strtopair_2_out_30), .out_31(strtopair_2_out_31), .out_32(strtopair_2_out_32));
  or or_13 (or_13_out, or_21_out, n8_bit_subtractor_1_out_18);
  or or_14 (or_14_out, or_22_out, n8_bit_subtractor_1_out_19);
  or or_15 (or_15_out, or_23_out, n8_bit_subtractor_1_out_20);
  or or_16 (or_16_out, or_24_out, n8_bit_subtractor_1_out_21);
  or or_17 (or_17_out, or_25_out, n8_bit_subtractor_1_out_22);
  or or_18 (or_18_out, or_26_out, n8_bit_subtractor_1_out_23);
  or or_19 (or_19_out, or_27_out, n8_bit_subtractor_1_out_24);
  or or_20 (or_20_out, or_28_out, n8_bit_subtractor_1_out_25);
  _8_bit_subtractor u_8_bit_subtractor_1 (
    .in_2(strtopair_2_out_17), .in_3(strtopair_2_out_25), .in_4(strtopair_2_out_18),
    .in_5(strtopair_2_out_26), .in_6(strtopair_2_out_19), .in_7(strtopair_2_out_27),
    .in_8(strtopair_2_out_20), .in_9(strtopair_2_out_28), .in_10(strtopair_2_out_21),
    .in_11(strtopair_2_out_29), .in_12(strtopair_2_out_22), .in_13(strtopair_2_out_30),
    .in_14(strtopair_2_out_23), .in_15(strtopair_2_out_31), .in_16(strtopair_2_out_24),
    .in_17(strtopair_2_out_32), .in_1(and_1_out), .out_26(n8_bit_subtractor_1_out_26),
    .out_18(n8_bit_subtractor_1_out_18), .out_19(n8_bit_subtractor_1_out_19),
    .out_20(n8_bit_subtractor_1_out_20), .out_21(n8_bit_subtractor_1_out_21),
    .out_22(n8_bit_subtractor_1_out_22), .out_23(n8_bit_subtractor_1_out_23),
    .out_24(n8_bit_subtractor_1_out_24), .out_25(n8_bit_subtractor_1_out_25));
  or or_21 (or_21_out, or_29_out, a_b_1_out_17);
  or or_22 (or_22_out, or_30_out, a_b_1_out_18);
  or or_23 (or_23_out, or_31_out, a_b_1_out_19);
  or or_24 (or_24_out, or_32_out, a_b_1_out_20);
  or or_25 (or_25_out, or_33_out, a_b_1_out_21);
  or or_26 (or_26_out, or_34_out, a_b_1_out_22);
  or or_27 (or_27_out, or_35_out, a_b_1_out_23);
  or or_28 (or_28_out, or_36_out, a_b_1_out_24);
  STRtoPAIR strtopair_3 (
    .in_1(n8_bit_blocker_alu_3_out_18), .in_2(n8_bit_blocker_alu_3_out_20),
    .in_3(n8_bit_blocker_alu_3_out_22), .in_4(n8_bit_blocker_alu_3_out_24),
    .in_5(n8_bit_blocker_alu_3_out_26), .in_6(n8_bit_blocker_alu_3_out_28),
    .in_7(n8_bit_blocker_alu_3_out_30), .in_8(n8_bit_blocker_alu_3_out_32),
    .in_9(n8_bit_blocker_alu_3_out_19), .in_10(n8_bit_blocker_alu_3_out_21),
    .in_11(n8_bit_blocker_alu_3_out_23), .in_12(n8_bit_blocker_alu_3_out_25),
    .in_13(n8_bit_blocker_alu_3_out_27), .in_14(n8_bit_blocker_alu_3_out_29),
    .in_15(n8_bit_blocker_alu_3_out_31), .in_16(n8_bit_blocker_alu_3_out_33), .out_17(strtopair_3_out_17),
    .out_18(strtopair_3_out_18), .out_19(strtopair_3_out_19), .out_20(strtopair_3_out_20),
    .out_21(strtopair_3_out_21), .out_22(strtopair_3_out_22), .out_23(strtopair_3_out_23),
    .out_24(strtopair_3_out_24), .out_25(strtopair_3_out_25), .out_26(strtopair_3_out_26),
    .out_27(strtopair_3_out_27), .out_28(strtopair_3_out_28), .out_29(strtopair_3_out_29),
    .out_30(strtopair_3_out_30), .out_31(strtopair_3_out_31), .out_32(strtopair_3_out_32));
  _8_bit_blocker_ALU u_8_bit_blocker_alu_3 (
    .in_9(n4_bit_multiplexer_1_out_8), .out_18(n8_bit_blocker_alu_3_out_18),
    .out_19(n8_bit_blocker_alu_3_out_19), .out_20(n8_bit_blocker_alu_3_out_20),
    .out_21(n8_bit_blocker_alu_3_out_21), .out_22(n8_bit_blocker_alu_3_out_22),
    .out_23(n8_bit_blocker_alu_3_out_23), .out_24(n8_bit_blocker_alu_3_out_24),
    .out_25(n8_bit_blocker_alu_3_out_25), .out_26(n8_bit_blocker_alu_3_out_26),
    .out_27(n8_bit_blocker_alu_3_out_27), .out_28(n8_bit_blocker_alu_3_out_28),
    .out_29(n8_bit_blocker_alu_3_out_29), .out_30(n8_bit_blocker_alu_3_out_30),
    .out_31(n8_bit_blocker_alu_3_out_31), .out_32(n8_bit_blocker_alu_3_out_32),
    .out_33(n8_bit_blocker_alu_3_out_33), .in_1(in_8), .in_2(in_7), .in_3(in_6), .in_4(in_5), .in_5(in_4),
    .in_6(in_3), .in_7(in_2), .in_8(A), .in_10(B), .in_11(in_10), .in_12(in_11), .in_13(in_12),
    .in_14(in_13), .in_15(in_14), .in_16(in_15), .in_17(in_16));
  A___B_2 a_b_1 (
    .in_1(strtopair_3_out_17), .in_2(strtopair_3_out_25), .in_3(strtopair_3_out_18),
    .in_4(strtopair_3_out_26), .in_5(strtopair_3_out_19), .in_6(strtopair_3_out_27),
    .in_7(strtopair_3_out_20), .in_8(strtopair_3_out_28), .in_9(strtopair_3_out_21),
    .in_10(strtopair_3_out_29), .in_11(strtopair_3_out_22), .in_12(strtopair_3_out_30),
    .in_13(strtopair_3_out_23), .in_14(strtopair_3_out_31), .in_15(strtopair_3_out_24),
    .in_16(strtopair_3_out_32), .out_17(a_b_1_out_17), .out_18(a_b_1_out_18), .out_19(a_b_1_out_19),
    .out_20(a_b_1_out_20), .out_21(a_b_1_out_21), .out_22(a_b_1_out_22), .out_23(a_b_1_out_23),
    .out_24(a_b_1_out_24));
  _8_bit_blocker_ALU u_8_bit_blocker_alu_4 (
    .in_9(n4_bit_multiplexer_1_out_9), .out_18(n8_bit_blocker_alu_4_out_18),
    .out_19(n8_bit_blocker_alu_4_out_19), .out_20(n8_bit_blocker_alu_4_out_20),
    .out_21(n8_bit_blocker_alu_4_out_21), .out_22(n8_bit_blocker_alu_4_out_22),
    .out_23(n8_bit_blocker_alu_4_out_23), .out_24(n8_bit_blocker_alu_4_out_24),
    .out_25(n8_bit_blocker_alu_4_out_25), .out_26(n8_bit_blocker_alu_4_out_26),
    .out_27(n8_bit_blocker_alu_4_out_27), .out_28(n8_bit_blocker_alu_4_out_28),
    .out_29(n8_bit_blocker_alu_4_out_29), .out_30(n8_bit_blocker_alu_4_out_30),
    .out_31(n8_bit_blocker_alu_4_out_31), .out_32(n8_bit_blocker_alu_4_out_32),
    .out_33(n8_bit_blocker_alu_4_out_33), .in_1(in_8), .in_2(in_7), .in_3(in_6), .in_4(in_5), .in_5(in_4),
    .in_6(in_3), .in_7(in_2), .in_8(A), .in_10(B), .in_11(in_10), .in_12(in_11), .in_13(in_12),
    .in_14(in_13), .in_15(in_14), .in_16(in_15), .in_17(in_16));
  or or_29 (or_29_out, or_37_out, a_b_2_out_17);
  or or_30 (or_30_out, or_38_out, a_b_2_out_18);
  or or_31 (or_31_out, or_39_out, a_b_2_out_19);
  or or_32 (or_32_out, or_40_out, a_b_2_out_20);
  or or_33 (or_33_out, or_41_out, a_b_2_out_21);
  or or_34 (or_34_out, or_42_out, a_b_2_out_22);
  or or_35 (or_35_out, or_43_out, a_b_2_out_23);
  or or_36 (or_36_out, or_44_out, a_b_2_out_24);
  STRtoPAIR strtopair_4 (
    .in_1(n8_bit_blocker_alu_4_out_18), .in_2(n8_bit_blocker_alu_4_out_20),
    .in_3(n8_bit_blocker_alu_4_out_22), .in_4(n8_bit_blocker_alu_4_out_24),
    .in_5(n8_bit_blocker_alu_4_out_26), .in_6(n8_bit_blocker_alu_4_out_28),
    .in_7(n8_bit_blocker_alu_4_out_30), .in_8(n8_bit_blocker_alu_4_out_32),
    .in_9(n8_bit_blocker_alu_4_out_19), .in_10(n8_bit_blocker_alu_4_out_21),
    .in_11(n8_bit_blocker_alu_4_out_23), .in_12(n8_bit_blocker_alu_4_out_25),
    .in_13(n8_bit_blocker_alu_4_out_27), .in_14(n8_bit_blocker_alu_4_out_29),
    .in_15(n8_bit_blocker_alu_4_out_31), .in_16(n8_bit_blocker_alu_4_out_33), .out_17(strtopair_4_out_17),
    .out_18(strtopair_4_out_18), .out_19(strtopair_4_out_19), .out_20(strtopair_4_out_20),
    .out_21(strtopair_4_out_21), .out_22(strtopair_4_out_22), .out_23(strtopair_4_out_23),
    .out_24(strtopair_4_out_24), .out_25(strtopair_4_out_25), .out_26(strtopair_4_out_26),
    .out_27(strtopair_4_out_27), .out_28(strtopair_4_out_28), .out_29(strtopair_4_out_29),
    .out_30(strtopair_4_out_30), .out_31(strtopair_4_out_31), .out_32(strtopair_4_out_32));
  A___B a_b_2 (
    .in_1(strtopair_4_out_17), .in_2(strtopair_4_out_25), .in_3(strtopair_4_out_18),
    .in_4(strtopair_4_out_26), .in_5(strtopair_4_out_19), .in_6(strtopair_4_out_27),
    .in_7(strtopair_4_out_20), .in_8(strtopair_4_out_28), .in_9(strtopair_4_out_21),
    .in_10(strtopair_4_out_29), .in_11(strtopair_4_out_22), .in_12(strtopair_4_out_30),
    .in_13(strtopair_4_out_23), .in_14(strtopair_4_out_31), .in_15(strtopair_4_out_24),
    .in_16(strtopair_4_out_32), .out_17(a_b_2_out_17), .out_18(a_b_2_out_18), .out_19(a_b_2_out_19),
    .out_20(a_b_2_out_20), .out_21(a_b_2_out_21), .out_22(a_b_2_out_22), .out_23(a_b_2_out_23),
    .out_24(a_b_2_out_24));
  or or_37 (or_37_out, or_45_out, XOR_out_17);
  or or_38 (or_38_out, or_46_out, XOR_out_18);
  or or_39 (or_39_out, or_47_out, XOR_out_19);
  or or_40 (or_40_out, or_48_out, XOR_out_20);
  or or_41 (or_41_out, or_49_out, XOR_out_21);
  or or_42 (or_42_out, or_50_out, XOR_out_22);
  or or_43 (or_43_out, or_51_out, XOR_out_23);
  or or_44 (or_44_out, or_52_out, XOR_out_24);
  _8_bit_blocker_ALU u_8_bit_blocker_alu_5 (
    .in_9(n4_bit_multiplexer_1_out_10), .out_18(n8_bit_blocker_alu_5_out_18),
    .out_19(n8_bit_blocker_alu_5_out_19), .out_20(n8_bit_blocker_alu_5_out_20),
    .out_21(n8_bit_blocker_alu_5_out_21), .out_22(n8_bit_blocker_alu_5_out_22),
    .out_23(n8_bit_blocker_alu_5_out_23), .out_24(n8_bit_blocker_alu_5_out_24),
    .out_25(n8_bit_blocker_alu_5_out_25), .out_26(n8_bit_blocker_alu_5_out_26),
    .out_27(n8_bit_blocker_alu_5_out_27), .out_28(n8_bit_blocker_alu_5_out_28),
    .out_29(n8_bit_blocker_alu_5_out_29), .out_30(n8_bit_blocker_alu_5_out_30),
    .out_31(n8_bit_blocker_alu_5_out_31), .out_32(n8_bit_blocker_alu_5_out_32),
    .out_33(n8_bit_blocker_alu_5_out_33), .in_1(in_8), .in_2(in_7), .in_3(in_6), .in_4(in_5), .in_5(in_4),
    .in_6(in_3), .in_7(in_2), .in_8(A), .in_10(B), .in_11(in_10), .in_12(in_11), .in_13(in_12),
    .in_14(in_13), .in_15(in_14), .in_16(in_15), .in_17(in_16));
  STRtoPAIR strtopair_5 (
    .in_1(n8_bit_blocker_alu_5_out_18), .in_2(n8_bit_blocker_alu_5_out_20),
    .in_3(n8_bit_blocker_alu_5_out_22), .in_4(n8_bit_blocker_alu_5_out_24),
    .in_5(n8_bit_blocker_alu_5_out_26), .in_6(n8_bit_blocker_alu_5_out_28),
    .in_7(n8_bit_blocker_alu_5_out_30), .in_8(n8_bit_blocker_alu_5_out_32),
    .in_9(n8_bit_blocker_alu_5_out_19), .in_10(n8_bit_blocker_alu_5_out_21),
    .in_11(n8_bit_blocker_alu_5_out_23), .in_12(n8_bit_blocker_alu_5_out_25),
    .in_13(n8_bit_blocker_alu_5_out_27), .in_14(n8_bit_blocker_alu_5_out_29),
    .in_15(n8_bit_blocker_alu_5_out_31), .in_16(n8_bit_blocker_alu_5_out_33), .out_17(strtopair_5_out_17),
    .out_18(strtopair_5_out_18), .out_19(strtopair_5_out_19), .out_20(strtopair_5_out_20),
    .out_21(strtopair_5_out_21), .out_22(strtopair_5_out_22), .out_23(strtopair_5_out_23),
    .out_24(strtopair_5_out_24), .out_25(strtopair_5_out_25), .out_26(strtopair_5_out_26),
    .out_27(strtopair_5_out_27), .out_28(strtopair_5_out_28), .out_29(strtopair_5_out_29),
    .out_30(strtopair_5_out_30), .out_31(strtopair_5_out_31), .out_32(strtopair_5_out_32));
  A_Xor_B XOR (
    .in_1(strtopair_5_out_17), .in_2(strtopair_5_out_25), .in_3(strtopair_5_out_18),
    .in_4(strtopair_5_out_26), .in_5(strtopair_5_out_19), .in_6(strtopair_5_out_27),
    .in_7(strtopair_5_out_20), .in_8(strtopair_5_out_28), .in_9(strtopair_5_out_21),
    .in_10(strtopair_5_out_29), .in_11(strtopair_5_out_22), .in_12(strtopair_5_out_30),
    .in_13(strtopair_5_out_23), .in_14(strtopair_5_out_31), .in_15(strtopair_5_out_24),
    .in_16(strtopair_5_out_32), .out_17(XOR_out_17), .out_18(XOR_out_18), .out_19(XOR_out_19),
    .out_20(XOR_out_20), .out_21(XOR_out_21), .out_22(XOR_out_22), .out_23(XOR_out_23), .out_24(XOR_out_24));
  or or_45 (or_45_out, or_53_out, n8_bit_blocker_alu_6_out_18);
  or or_46 (or_46_out, or_54_out, n8_bit_blocker_alu_6_out_19);
  or or_47 (or_47_out, or_55_out, n8_bit_blocker_alu_6_out_20);
  or or_48 (or_48_out, or_56_out, n8_bit_blocker_alu_6_out_21);
  or or_49 (or_49_out, or_57_out, n8_bit_blocker_alu_6_out_22);
  or or_50 (or_50_out, or_58_out, n8_bit_blocker_alu_6_out_23);
  or or_51 (or_51_out, or_59_out, n8_bit_blocker_alu_6_out_24);
  or or_52 (or_52_out, or_60_out, n8_bit_blocker_alu_6_out_25);
  circuit part_1 (
    .in_1(A), .in_2(in_2), .in_3(in_3), .in_4(in_4), .in_5(in_5), .in_6(in_6), .in_7(in_7), .in_8(in_8),
    .out_9(part_1_out_9), .out_10(part_1_out_10), .out_11(part_1_out_11), .out_12(part_1_out_12),
    .out_13(part_1_out_13), .out_14(part_1_out_14), .out_15(part_1_out_15), .out_16(part_1_out_16));
  _8_bit_blocker_ALU u_8_bit_blocker_alu_6 (
    .in_9(n4_bit_multiplexer_1_out_11), .out_18(n8_bit_blocker_alu_6_out_18),
    .out_19(n8_bit_blocker_alu_6_out_19), .out_20(n8_bit_blocker_alu_6_out_20),
    .out_21(n8_bit_blocker_alu_6_out_21), .out_22(n8_bit_blocker_alu_6_out_22),
    .out_23(n8_bit_blocker_alu_6_out_23), .out_24(n8_bit_blocker_alu_6_out_24),
    .out_25(n8_bit_blocker_alu_6_out_25), .in_1(part_1_out_16), .in_2(part_1_out_15), .in_3(part_1_out_14),
    .in_4(part_1_out_13), .in_5(part_1_out_12), .in_6(part_1_out_11), .in_7(part_1_out_10),
    .in_8(part_1_out_9));  // open: out_26, out_27, out_28, out_29, out_30, out_31, out_32, out_33, in_10, in_11, in_12, in_13, in_14, in_15, in_16, in_17
  or or_53 (or_53_out, or_61_out, n8_bit_blocker_alu_7_out_26);
  or or_54 (or_54_out, or_62_out, n8_bit_blocker_alu_7_out_27);
  or or_55 (or_55_out, or_63_out, n8_bit_blocker_alu_7_out_28);
  or or_56 (or_56_out, or_64_out, n8_bit_blocker_alu_7_out_29);
  or or_57 (or_57_out, or_65_out, n8_bit_blocker_alu_7_out_30);
  or or_58 (or_58_out, or_66_out, n8_bit_blocker_alu_7_out_31);
  or or_59 (or_59_out, or_67_out, n8_bit_blocker_alu_7_out_32);
  or or_60 (or_60_out, or_68_out, n8_bit_blocker_alu_7_out_33);
  circuit part_2 (
    .in_1(B), .in_2(in_10), .in_3(in_11), .in_4(in_12), .in_5(in_13), .in_6(in_14), .in_7(in_15),
    .in_8(in_16), .out_9(part_2_out_9), .out_10(part_2_out_10), .out_11(part_2_out_11),
    .out_12(part_2_out_12), .out_13(part_2_out_13), .out_14(part_2_out_14), .out_15(part_2_out_15),
    .out_16(part_2_out_16));
  _8_bit_blocker_ALU u_8_bit_blocker_alu_7 (
    .in_9(n4_bit_multiplexer_1_out_12), .out_26(n8_bit_blocker_alu_7_out_26),
    .out_27(n8_bit_blocker_alu_7_out_27), .out_28(n8_bit_blocker_alu_7_out_28),
    .out_29(n8_bit_blocker_alu_7_out_29), .out_30(n8_bit_blocker_alu_7_out_30),
    .out_31(n8_bit_blocker_alu_7_out_31), .out_32(n8_bit_blocker_alu_7_out_32),
    .out_33(n8_bit_blocker_alu_7_out_33), .in_10(part_2_out_9), .in_11(part_2_out_10), .in_12(part_2_out_11),
    .in_13(part_2_out_12), .in_14(part_2_out_13), .in_15(part_2_out_14), .in_16(part_2_out_15),
    .in_17(part_2_out_16));  // open: out_18, out_19, out_20, out_21, out_22, out_23, out_24, out_25, in_1, in_2, in_3, in_4, in_5, in_6, in_7, in_8
  bit_shifter bit_shifter_1 (
    .in_1(n8_bit_blocker_alu_8_out_25), .in_2(n8_bit_blocker_alu_8_out_24),
    .in_3(n8_bit_blocker_alu_8_out_23), .in_4(n8_bit_blocker_alu_8_out_22),
    .in_5(n8_bit_blocker_alu_8_out_21), .in_6(n8_bit_blocker_alu_8_out_20),
    .in_7(n8_bit_blocker_alu_8_out_19), .in_8(n8_bit_blocker_alu_8_out_18),
    .in_9(n8_bit_blocker_alu_8_out_28), .in_10(n8_bit_blocker_alu_8_out_27),
    .in_11(n8_bit_blocker_alu_8_out_26), .out_12(bit_shifter_1_out_12), .out_13(bit_shifter_1_out_13),
    .out_14(bit_shifter_1_out_14), .out_15(bit_shifter_1_out_15), .out_16(bit_shifter_1_out_16),
    .out_17(bit_shifter_1_out_17), .out_18(bit_shifter_1_out_18), .out_19(bit_shifter_1_out_19));
  _8_bit_blocker_ALU u_8_bit_blocker_alu_8 (
    .in_9(n4_bit_multiplexer_1_out_13), .out_18(n8_bit_blocker_alu_8_out_18),
    .out_19(n8_bit_blocker_alu_8_out_19), .out_20(n8_bit_blocker_alu_8_out_20),
    .out_21(n8_bit_blocker_alu_8_out_21), .out_22(n8_bit_blocker_alu_8_out_22),
    .out_23(n8_bit_blocker_alu_8_out_23), .out_24(n8_bit_blocker_alu_8_out_24),
    .out_25(n8_bit_blocker_alu_8_out_25), .out_26(n8_bit_blocker_alu_8_out_26),
    .out_27(n8_bit_blocker_alu_8_out_27), .out_28(n8_bit_blocker_alu_8_out_28), .in_1(in_8), .in_2(in_7),
    .in_3(in_6), .in_4(in_5), .in_5(in_4), .in_6(in_3), .in_7(in_2), .in_8(A), .in_10(B), .in_11(in_10),
    .in_12(in_11));  // open: out_29, out_30, out_31, out_32, out_33, in_13, in_14, in_15, in_16, in_17
  or or_61 (or_61_out, or_69_out, bit_shifter_1_out_19);
  or or_62 (or_62_out, or_70_out, bit_shifter_1_out_18);
  or or_63 (or_63_out, or_71_out, bit_shifter_1_out_17);
  or or_64 (or_64_out, or_72_out, bit_shifter_1_out_16);
  or or_65 (or_65_out, or_73_out, bit_shifter_1_out_15);
  or or_66 (or_66_out, or_74_out, bit_shifter_1_out_14);
  or or_67 (or_67_out, or_75_out, bit_shifter_1_out_13);
  or or_68 (or_68_out, or_76_out, bit_shifter_1_out_12);
  or or_69 (or_69_out, or_77_out, bit_shifter_2_out_19);
  or or_70 (or_70_out, or_79_out, bit_shifter_2_out_18);
  or or_71 (or_71_out, or_80_out, bit_shifter_2_out_17);
  or or_72 (or_72_out, or_81_out, bit_shifter_2_out_16);
  or or_73 (or_73_out, or_82_out, bit_shifter_2_out_15);
  or or_74 (or_74_out, or_83_out, bit_shifter_2_out_14);
  or or_75 (or_75_out, or_84_out, bit_shifter_2_out_13);
  or or_76 (or_76_out, or_85_out, bit_shifter_2_out_12);
  _8_bit_blocker_ALU u_8_bit_blocker_alu_9 (
    .in_9(n4_bit_multiplexer_1_out_14), .out_18(n8_bit_blocker_alu_9_out_18),
    .out_19(n8_bit_blocker_alu_9_out_19), .out_20(n8_bit_blocker_alu_9_out_20),
    .out_21(n8_bit_blocker_alu_9_out_21), .out_22(n8_bit_blocker_alu_9_out_22),
    .out_23(n8_bit_blocker_alu_9_out_23), .out_24(n8_bit_blocker_alu_9_out_24),
    .out_25(n8_bit_blocker_alu_9_out_25), .out_26(n8_bit_blocker_alu_9_out_26),
    .out_27(n8_bit_blocker_alu_9_out_27), .out_28(n8_bit_blocker_alu_9_out_28), .in_1(in_8), .in_2(in_7),
    .in_3(in_6), .in_4(in_5), .in_5(in_4), .in_6(in_3), .in_7(in_2), .in_8(A), .in_10(B), .in_11(in_10),
    .in_12(in_11));  // open: out_29, out_30, out_31, out_32, out_33, in_13, in_14, in_15, in_16, in_17
  bit_shifter_2 bit_shifter_2 (
    .out_12(bit_shifter_2_out_12), .out_13(bit_shifter_2_out_13), .out_14(bit_shifter_2_out_14),
    .out_15(bit_shifter_2_out_15), .out_16(bit_shifter_2_out_16), .out_17(bit_shifter_2_out_17),
    .out_18(bit_shifter_2_out_18), .out_19(bit_shifter_2_out_19), .in_9(n8_bit_blocker_alu_9_out_28),
    .in_1(n8_bit_blocker_alu_9_out_25), .in_2(n8_bit_blocker_alu_9_out_24),
    .in_3(n8_bit_blocker_alu_9_out_23), .in_4(n8_bit_blocker_alu_9_out_22),
    .in_5(n8_bit_blocker_alu_9_out_21), .in_6(n8_bit_blocker_alu_9_out_20),
    .in_7(n8_bit_blocker_alu_9_out_19), .in_8(n8_bit_blocker_alu_9_out_18),
    .in_10(n8_bit_blocker_alu_9_out_27), .in_11(n8_bit_blocker_alu_9_out_26));
  _8_bit_blocker_ALU u_8_bit_blocker_alu_10 (
    .in_9(n4_bit_multiplexer_1_out_15), .out_18(n8_bit_blocker_alu_10_out_18),
    .out_19(n8_bit_blocker_alu_10_out_19), .out_20(n8_bit_blocker_alu_10_out_20),
    .out_21(n8_bit_blocker_alu_10_out_21), .out_22(n8_bit_blocker_alu_10_out_22),
    .out_23(n8_bit_blocker_alu_10_out_23), .out_24(n8_bit_blocker_alu_10_out_24),
    .out_25(n8_bit_blocker_alu_10_out_25), .out_26(n8_bit_blocker_alu_10_out_26),
    .out_27(n8_bit_blocker_alu_10_out_27), .out_28(n8_bit_blocker_alu_10_out_28),
    .out_29(n8_bit_blocker_alu_10_out_29), .out_30(n8_bit_blocker_alu_10_out_30),
    .out_31(n8_bit_blocker_alu_10_out_31), .out_32(n8_bit_blocker_alu_10_out_32),
    .out_33(n8_bit_blocker_alu_10_out_33), .in_1(in_8), .in_2(in_7), .in_3(in_6), .in_4(in_5), .in_5(in_4),
    .in_6(in_3), .in_7(in_2), .in_8(A), .in_10(B), .in_11(in_10), .in_12(in_11), .in_13(in_12),
    .in_14(in_13), .in_15(in_14), .in_16(in_15), .in_17(in_16));
  STRtoPAIR strtopair_6 (
    .in_1(n8_bit_blocker_alu_10_out_18), .in_2(n8_bit_blocker_alu_10_out_20),
    .in_3(n8_bit_blocker_alu_10_out_22), .in_4(n8_bit_blocker_alu_10_out_24),
    .in_5(n8_bit_blocker_alu_10_out_26), .in_6(n8_bit_blocker_alu_10_out_28),
    .in_7(n8_bit_blocker_alu_10_out_30), .in_8(n8_bit_blocker_alu_10_out_32),
    .in_9(n8_bit_blocker_alu_10_out_19), .in_10(n8_bit_blocker_alu_10_out_21),
    .in_11(n8_bit_blocker_alu_10_out_23), .in_12(n8_bit_blocker_alu_10_out_25),
    .in_13(n8_bit_blocker_alu_10_out_27), .in_14(n8_bit_blocker_alu_10_out_29),
    .in_15(n8_bit_blocker_alu_10_out_31), .in_16(n8_bit_blocker_alu_10_out_33), .out_17(strtopair_6_out_17),
    .out_18(strtopair_6_out_18), .out_19(strtopair_6_out_19), .out_20(strtopair_6_out_20),
    .out_21(strtopair_6_out_21), .out_22(strtopair_6_out_22), .out_23(strtopair_6_out_23),
    .out_24(strtopair_6_out_24), .out_25(strtopair_6_out_25), .out_26(strtopair_6_out_26),
    .out_27(strtopair_6_out_27), .out_28(strtopair_6_out_28), .out_29(strtopair_6_out_29),
    .out_30(strtopair_6_out_30), .out_31(strtopair_6_out_31), .out_32(strtopair_6_out_32));
  buf or_77 (or_77_out, or_78_out);  // OR_Gate
  COMP COMP (
    .in_1(strtopair_6_out_17), .in_2(strtopair_6_out_25), .in_3(strtopair_6_out_18),
    .in_4(strtopair_6_out_26), .in_5(strtopair_6_out_19), .in_6(strtopair_6_out_27),
    .in_7(strtopair_6_out_20), .in_8(strtopair_6_out_28), .in_9(strtopair_6_out_21),
    .in_10(strtopair_6_out_29), .in_11(strtopair_6_out_22), .in_12(strtopair_6_out_30),
    .in_13(strtopair_6_out_23), .in_14(strtopair_6_out_31), .in_15(strtopair_6_out_24),
    .in_16(strtopair_6_out_32), .out_17(ZERO_flag));
  or or_78 (or_78_out, or_86_out, mult_out_17);
  or or_79 (or_79_out, 1'b0, mult_out_18);
  or or_80 (or_80_out, 1'b0, mult_out_19);
  or or_81 (or_81_out, 1'b0, mult_out_20);
  or or_82 (or_82_out, 1'b0, mult_out_21);
  or or_83 (or_83_out, 1'b0, mult_out_22);
  or or_84 (or_84_out, 1'b0, mult_out_23);
  or or_85 (or_85_out, 1'b0, mult_out_24);
  _8_bit_blocker_ALU u_8_bit_blocker_alu_11 (
    .in_9(n4_bit_multiplexer_1_out_17), .out_18(n8_bit_blocker_alu_11_out_18),
    .out_19(n8_bit_blocker_alu_11_out_19), .out_20(n8_bit_blocker_alu_11_out_20),
    .out_21(n8_bit_blocker_alu_11_out_21), .out_22(n8_bit_blocker_alu_11_out_22),
    .out_23(n8_bit_blocker_alu_11_out_23), .out_24(n8_bit_blocker_alu_11_out_24),
    .out_25(n8_bit_blocker_alu_11_out_25), .out_26(n8_bit_blocker_alu_11_out_26),
    .out_27(n8_bit_blocker_alu_11_out_27), .out_28(n8_bit_blocker_alu_11_out_28),
    .out_29(n8_bit_blocker_alu_11_out_29), .out_30(n8_bit_blocker_alu_11_out_30),
    .out_31(n8_bit_blocker_alu_11_out_31), .out_32(n8_bit_blocker_alu_11_out_32),
    .out_33(n8_bit_blocker_alu_11_out_33), .in_1(in_8), .in_2(in_7), .in_3(in_6), .in_4(in_5), .in_5(in_4),
    .in_6(in_3), .in_7(in_2), .in_8(A), .in_10(B), .in_11(in_10), .in_12(in_11), .in_13(in_12),
    .in_14(in_13), .in_15(in_14), .in_16(in_15), .in_17(in_16));
  mult mult (
    .in_1(n8_bit_blocker_alu_11_out_18), .in_2(n8_bit_blocker_alu_11_out_19),
    .in_3(n8_bit_blocker_alu_11_out_20), .in_4(n8_bit_blocker_alu_11_out_21),
    .in_5(n8_bit_blocker_alu_11_out_22), .in_6(n8_bit_blocker_alu_11_out_23),
    .in_7(n8_bit_blocker_alu_11_out_24), .in_8(n8_bit_blocker_alu_11_out_25),
    .in_9(n8_bit_blocker_alu_11_out_26), .in_10(n8_bit_blocker_alu_11_out_27),
    .in_11(n8_bit_blocker_alu_11_out_28), .in_12(n8_bit_blocker_alu_11_out_29),
    .in_13(n8_bit_blocker_alu_11_out_30), .in_14(n8_bit_blocker_alu_11_out_31),
    .in_15(n8_bit_blocker_alu_11_out_32), .in_16(n8_bit_blocker_alu_11_out_33), .out_17(mult_out_17),
    .out_18(mult_out_18), .out_19(mult_out_19), .out_20(mult_out_20), .out_21(mult_out_21),
    .out_22(mult_out_22), .out_23(mult_out_23), .out_24(mult_out_24));
  or or_86 (or_86_out, 1'b0, if_odd_1_out_9);
  _8_bit_blocker_ALU u_8_bit_blocker_alu_12 (
    .in_9(n4_bit_multiplexer_1_out_18), .out_18(n8_bit_blocker_alu_12_out_18),
    .out_19(n8_bit_blocker_alu_12_out_19), .out_20(n8_bit_blocker_alu_12_out_20),
    .out_21(n8_bit_blocker_alu_12_out_21), .out_22(n8_bit_blocker_alu_12_out_22),
    .out_23(n8_bit_blocker_alu_12_out_23), .out_24(n8_bit_blocker_alu_12_out_24),
    .out_25(n8_bit_blocker_alu_12_out_25), .in_1(in_8), .in_2(in_7), .in_3(in_6), .in_4(in_5), .in_5(in_4),
    .in_6(in_3), .in_7(in_2), .in_8(A));  // open: out_26, out_27, out_28, out_29, out_30, out_31, out_32, out_33, in_10, in_11, in_12, in_13, in_14, in_15, in_16, in_17
  IF_ODD if_odd_1 (
    .in_1(n8_bit_blocker_alu_12_out_18), .in_2(n8_bit_blocker_alu_12_out_19),
    .in_3(n8_bit_blocker_alu_12_out_20), .in_4(n8_bit_blocker_alu_12_out_21),
    .in_5(n8_bit_blocker_alu_12_out_22), .in_6(n8_bit_blocker_alu_12_out_23),
    .in_7(n8_bit_blocker_alu_12_out_24), .in_8(n8_bit_blocker_alu_12_out_25), .out_9(if_odd_1_out_9));
endmodule

module experimentation (
  input  _1,
  input  _2,
  input  _4,
  input  _8,
  input  _16,
  input  _32,
  input  _64,
  input  _128,
  input  in_9,
  input  _1_2,
  input  _1_3,
  input  _2_2,
  input  _2_3,
  input  _4_2,
  input  _4_3,
  input  _8_2,
  input  _8_3,
  input  _16_2,
  input  _16_3,
  input  _32_2,
  input  _32_3,
  input  _64_2,
  input  _64_3,
  input  _128_2,
  input  _128_3,
  output _1_4,
  output _2_4,
  output _4_4,
  output _8_4,
  output _16_4,
  output _32_4,
  output _64_4,
  output _128_4,
  output out_34,
  output out_35,
  output out_36,
  output out_37,
  output out_38,
  output out_39,
  output out_40,
  output out_41
);

  circuit_2_2 part_1 (
    .in_1(_128), .in_2(_64), .in_3(_32), .in_4(_16), .in_5(_8), .in_6(_4), .in_7(_2), .in_8(_1),
    .out_9(_128_4), .out_10(_64_4), .out_11(_32_4), .out_12(_16_4), .out_13(_8_4), .out_14(_4_4),
    .out_15(_2_4), .out_16(_1_4));
  _8_bit_adder u_8_bit_adder_1 (
    .in_2(_1_2), ._1(_1_3), .in_4(_2_2), ._2(_2_3), .in_6(_4_2), ._4(_4_3), .in_8(_8_2), ._8(_8_3),
    .in_10(_16_2), ._16(_16_3), .in_12(_32_2), ._32(_32_3), .in_14(_64_2), ._64(_64_3), .in_16(_128_2),
    ._128(_128_3), .Cin(in_9), .out_18(out_34), .out_19(out_35), .out_20(out_36), .out_21(out_37),
    .out_22(out_38), .out_23(out_39), .out_24(out_40), .out_25(out_41));  // open: Cout
endmodule

module mult (
  input  in_1,
  input  in_2,
  input  in_3,
  input  in_4,
  input  in_5,
  input  in_6,
  input  in_7,
  input  in_8,
  input  in_9,
  input  in_10,
  input  in_11,
  input  in_12,
  input  in_13,
  input  in_14,
  input  in_15,
  input  in_16,
  output out_17,
  output out_18,
  output out_19,
  output out_20,
  output out_21,
  output out_22,
  output out_23,
  output out_24
);

  Multiplier multiplier_1 (
    .a({in_8, in_7, in_6, in_5, in_4, in_3, in_2, in_1}),
    .b({in_16, in_15, in_14, in_13, in_12, in_11, in_10, in_9}),
    .out({out_24, out_23, out_22, out_21, out_20, out_19, out_18, out_17}));  // open: cin, cout
endmodule

module COMP (
  input  in_1,
  input  in_2,
  input  in_3,
  input  in_4,
  input  in_5,
  input  in_6,
  input  in_7,
  input  in_8,
  input  in_9,
  input  in_10,
  input  in_11,
  input  in_12,
  input  in_13,
  input  in_14,
  input  in_15,
  input  in_16,
  output out_17
);

  wire n8_bit_subtractor_1_out_18, n8_bit_subtractor_1_out_19, n8_bit_subtractor_1_out_20,
       n8_bit_subtractor_1_out_21, n8_bit_subtractor_1_out_22, n8_bit_subtractor_1_out_23,
       n8_bit_subtractor_1_out_24, n8_bit_subtractor_1_out_25, n8_bit_subtractor_1_out_26, or_1_out;

  _8_bit_subtractor u_8_bit_subtractor_1 (
    .in_2(in_1), .in_3(in_2), .in_4(in_3), .in_5(in_4), .in_6(in_5), .in_7(in_6), .in_8(in_7), .in_9(in_8),
    .in_10(in_9), .in_11(in_10), .in_12(in_11), .in_13(in_12), .in_14(in_13), .in_15(in_14), .in_16(in_15),
    .in_17(in_16), .in_1(1'b0), .out_26(n8_bit_subtractor_1_out_26), .out_18(n8_bit_subtractor_1_out_18),
    .out_19(n8_bit_subtractor_1_out_19), .out_20(n8_bit_subtractor_1_out_20),
    .out_21(n8_bit_subtractor_1_out_21), .out_22(n8_bit_subtractor_1_out_22),
    .out_23(n8_bit_subtractor_1_out_23), .out_24(n8_bit_subtractor_1_out_24),
    .out_25(n8_bit_subtractor_1_out_25));
  not not_1 (out_17, or_1_out);
  or or_1 (or_1_out, n8_bit_subtractor_1_out_18, n8_bit_subtractor_1_out_19, n8_bit_subtractor_1_out_20, n8_bit_subtractor_1_out_21, n8_bit_subtractor_1_out_22, n8_bit_subtractor_1_out_23, n8_bit_subtractor_1_out_24, n8_bit_subtractor_1_out_25, n8_bit_subtractor_1_out_26);
endmodule

module program_counter (
  input  in_1,
  input  in_2,
  input  in_3,
  input  in_4,
  input  in_5,
  input  in_6,
  input  in_7,
  output out_8,
  output out_9,
  output out_10,
  output out_11
);

  wire clock_1_out;

  D_Flip_Flop d_ff_1 (.Q(out_8), .Qn(out_10), .preset(in_1), .reset(in_2));  // open: clk, D, en
  Counter counter_1 (.load(in_5), .count(in_6), .clk(clock_1_out), .clr(in_7));  // open: D, Q, carry
  Clock clock_1 (.out(clock_1_out));
  D_Flip_Flop d_ff_2 (.Q(out_9), .Qn(out_11), .preset(in_3), .reset(in_4));  // open: clk, D, en
endmodule
